// Logisim project ALU.circ as structural Verilog: 2 circuits, main circuit main
module main (
);

  wire clock_1_out;
  wire [6:0] counter_1_q;
  wire [7:0] rom_3_data;
  wire [15:0] alu_1_out_6, rom_1_data, rom_2_data;

  Counter #(.width(7), .max('h7f)) counter_1 (.Q(counter_1_q), .clk(clock_1_out));  // open: load, D, count, carry, clr
  Clock clock_1 (.out(clock_1_out));
  ROM #(.addrWidth(7), .dataWidth(16)) rom_1 (.addr(counter_1_q), .data(rom_1_data), .sel(1'b1));
  ROM #(.addrWidth(7), .dataWidth(16)) rom_2 (.addr(counter_1_q), .data(rom_2_data), .sel(1'b1));
  ROM #(.addrWidth(7)) rom_3 (.addr(counter_1_q), .data(rom_3_data), .sel(1'b1));
  // Probe on rom_3_data[3:0]
  ALU alu_1 (.in_1(rom_3_data[3:0]), .in_2(rom_1_data), .in_3(rom_2_data), .out_6(alu_1_out_6));  // open: out_4, out_5
  RAM #(.addrWidth(7), .dataWidth(16)) ram_1 (
    .addr(counter_1_q), .data(alu_1_out_6), .sel(1'b1), .clk(clock_1_out), .ld(1'b0));  // open: clr

  // Notes on the sheet:
  //   contents of rom_1 (hex, n*v repeats v):
  //   3756 15b6 28c8 f392 1e23 141a edf1 1b32 8bdb eb22 4c7e a8b2 4990 c38c a5d3 ef87 f5f3 b9eb 2274 6b17
  //   3f6e b26f 5873 7cb8 dc40 21fb 71e7 4d26 d679 c94a 942e ecca addd 9202 4958 ca5b 5e51 6ea8 788c 6235
  //   f9f 268 a3bc d357 796 5884 f5fd 26a6 8a28 8ce1 df7a 92ad c188 f1e0 2a4c 8107 9fcc 267c a3d2 ef06
  //   2c7b c526 6e3a 2eb7 5345 92b8 f6a0 cef8 df36 b865 70c6 e0d1 26c7 b9a9 7d26 c3f0 ebff a26a 21b7 981b
  //   5792 a4a3 1f0b 543c 4d52 3028 a8fd c0fa c719 3ca0 8c3 ae82 d3e2 f15f a59a d39f 345d ca2a 42e7 80e8
  //   a1f 645d 873b f171 2ffe 1b77 9f0d 9eb8 fef9 72b1 107f b969 3435 e032 4036 1347 95ff 89ac d27d b39e
  //   3e26 94fc 2aa7 78c1 6a47 f78 3c52
  //   contents of rom_2 (hex, n*v repeats v):
  //   f3ce e3b6 c9c9 db06 e034 251d 5 c 45c3 ab60 e024 2723 47a9 c0ed 71ae a 6 4b38 f2b5 2381 d0d7 def6 f
  //   d ad6f e f2e1 49a7 1 ce29 b ae65 2927 a 3 3 b9dd a fa8f ad02 9a97 76ff 3 5 2 4 d272 3018 2356 5c64
  //   af1d 4936 c107 247a 6 7 4803 9 de63 67eb 462b 3582 be11 17c8 2d67 6977 70a7 dde8 7 affe 52f8 98a7
  //   4263 4 42ec 1643 a f 1b33 626a 0 ae1e e b4 b13f e054 8 d8c3 93da d 1 2 c 8 2 5ab8 3ada 2821 d479 b
  //   802b 6ab8 8376 a977 d06 4777 55b6 bafd f146 4ef1 48c9 cdde a 1229 a16c ffcb 41f4 e6d3 4810 50c8 1
  //   b135 16a8 9 33b fec4 4
  //   contents of rom_3 (hex, n*v repeats v):
  //   2 1 5 5 2 6 8 8 5 7 6 0 5 0 5 a 8 5 5 7 5 2 8 b 5 8 4 7 a 2 8 0 2 8 8 b 0 a 3 7 4 0 b 8 a 9 3 0 4 4
  //   6 2 0 1 9 a 4 a 7 3 1 1 5 4 1 1 3 4 9 3 3 5 1 a 1 7 a a 0 5 9 0 b 7 3 7 8 3 7 a b b b a 9 4 3 3 4 9
  //   7 2 4 1 6 2 7 2 2 5 1 4 8 4 1 6 5 3 5 2 8 5 3 a 4 0 9
endmodule

module ALU (
  input  [3:0] in_1,
  input  [15:0] in_2,
  input  [15:0] in_3,
  output out_4,
  output out_5,
  output [15:0] out_6
);

  wire [15:0] Arithmetic_out, Logic_out, shifting_out;

  LogicUnit logicunit_1 (.BUS_A(in_2), .BUS_B(in_3), .Logic_control(in_1[1:0]), .Logic_unit_result(Logic_out));
  ShiftingUnitCircuit shiftingunitcircuit_1 (.Operand(in_2), .SA(in_3[3:0]), .OP(in_1[1:0]), .Operand_2(shifting_out));
  alu_arithmetic alu_arithmetic_1 (
    .Overflow(out_4), .Output(Arithmetic_out), .in_2(in_3), .in_3(in_2), .Zero(out_5), .Operation(in_1[1:0]));
  Multiplexer #(.select(2), .width(16), .enable("false")) multiplexer_1 (
    .in0(Logic_out), .in1(Arithmetic_out), .in2(shifting_out), .in3(shifting_out), .out(out_6),
    .sel(in_1[3:2]));

  // Other names for the same wires on the sheet: A[15:0] = in_2; B[15:0] = in_3; MainALU_output[15:0] = out_6;
  //   Operation[3:0] = in_1; sectionselc[1:0] = in_1[1:0]; Main_selc[1:0] = in_1[3:2]; overflow = out_4; zero = out_5
endmodule
