// Logisim project logicUnit.circ as structural Verilog: 1 circuit, main circuit LogicUnit
module LogicUnit (
  input  [15:0] BUS_A,
  input  [15:0] BUS_B,
  input  [1:0] Logic_control,
  output [15:0] Logic_unit_result
);

  wire [15:0] AND_out, NOR_out, OR_out, XOR_out;

  assign AND_out = BUS_A & BUS_B;  // AND_Gate and_1, 16 bits wide
  assign OR_out = BUS_A | BUS_B;  // OR_Gate or_1, 16 bits wide
  assign XOR_out = BUS_A ^ BUS_B;  // XOR_Gate xor_1, 16 bits wide
  assign NOR_out = ~(BUS_A | BUS_B);  // NOR_Gate nor_1, 16 bits wide
  Multiplexer #(.select(2), .width(16), .disabled(0), .enable("false")) multiplexer_1 (
    .in0(AND_out), .in1(OR_out), .in2(XOR_out), .in3(NOR_out), .out(Logic_unit_result), .sel(Logic_control));

  // Other names for the same wires on the sheet: A[15:0] = BUS_A; B[15:0] = BUS_B
endmodule
