// Logisim project ShiftingUnit.circ as structural Verilog: 1 circuit, main circuit ShiftingUnitCircuit
module ShiftingUnitCircuit (
  input  [15:0] Operand,
  input  [3:0] SA,
  input  [1:0] OP,
  output [15:0] Operand_2
);

  wire [15:0] ROR, SLL, SRLA;

  SLL sll_1 (.Operand(Operand), .Shift_Amount(SA), .Output(SLL));
  SRLA srla_1 (.Operand(Operand), .Shift_Amount(SA), .Arithmetic_Shift(OP[1]), .Output(SRLA));
  RotateRight rotateright_1 (.Operand(Operand), .SA(SA), .Operand_2(ROR));
  Multiplexer #(.select(2), .width(16), .enable("false")) multiplexer_1 (
    .in0(SLL), .in1(SRLA), .in2(SRLA), .in3(ROR), .out(Operand_2), .sel(OP));

  // Other names for the same wires on the sheet: Output[15:0] = Operand_2
endmodule
