// Logisim project ControlUnitC.circ as structural Verilog: 4 circuits, main circuit ControlUnit
module ControlUnit (
  input  [4:0] Opcode,
  input  [1:0] Function,
  output [3:0] ALUop,
  output ALUSrc,
  output signExtend,
  output RegWrite,
  output [1:0] RegDest,
  output [1:0] RegWSrc,
  output memoryRead,
  output memoryWrite,
  output [1:0] PCSrc,
  output [1:0] BrachOP,
  output JumpOP
);

  ALUControlUnit alucontrolunit_1 (
    .OP0(Opcode[0]), .OP1(Opcode[1]), .OP2(Opcode[2]), .OP3(Opcode[3]), .OP4(Opcode[4]), .F0(Function[0]),
    .F1(Function[1]), .ALUop0(ALUop[0]), .ALUop1(ALUop[1]), .ALUop2(ALUop[2]), .ALUop3(ALUop[3]),
    .ALUSrc(ALUSrc), .signExtend(signExtend));
  RegistersMemoryControlUnit registersmemorycontrolunit_1 (
    .OP3(Opcode[0]), .OP2(Opcode[1]), .OP1(Opcode[2]), .OP0(Opcode[3]), .RegDest1(RegWrite),
    .RegWSrc0(RegDest[0]), .memoryRead(RegWSrc[0]), .memoryWrite(RegWSrc[1]));  // open: OP4, RegWrite, RegDest0, RegWSrc1
  ProgramCounterControlUnit programcountercontrolunit_1 (
    .OP4(Opcode[0]), .OP3(Opcode[1]), .PCSrc0(PCSrc[0]), .OP2(Opcode[2]), .OP1(Opcode[3]), .OP0(Opcode[4]),
    .PCSrc1(PCSrc[1]), .BrachOP0(BrachOP[0]), .BranchOP1(BrachOP[1]), .JumpOP(JumpOP));
endmodule

module ALUControlUnit (
  input  OP0,
  input  OP1,
  input  OP2,
  input  OP3,
  input  OP4,
  input  F0,
  input  F1,
  output ALUop0,
  output ALUop1,
  output ALUop2,
  output ALUop3,
  output ALUSrc,
  output signExtend
);
endmodule

module RegistersMemoryControlUnit (
  input  OP4,
  input  OP3,
  input  OP2,
  input  OP1,
  input  OP0,
  output RegWrite,
  output RegDest1,
  output RegDest0,
  output RegWSrc1,
  output RegWSrc0,
  output memoryRead,
  output memoryWrite
);

  wire and_2_out, and_3_out, and_4_out, and_5_out, and_6_out, and_7_out, and_8_out, and_9_out, not_1_out,
       not_2_out, not_3_out, not_4_out, not_5_out, not_6_out, not_7_out, not_8_out, not_9_out, not_10_out,
       not_11_out, not_12_out, not_13_out, not_14_out, not_15_out;

  not not_1 (not_1_out, OP4);
  not not_2 (not_2_out, OP3);
  not not_3 (not_3_out, OP1);
  not not_4 (not_4_out, OP4);
  not not_5 (not_5_out, OP1);
  not not_6 (not_6_out, OP0);
  not not_7 (not_7_out, OP3);
  not not_8 (not_8_out, OP2);
  not not_9 (not_9_out, OP3);
  not not_10 (not_10_out, OP3);
  not not_11 (not_11_out, OP2);
  not not_12 (not_12_out, OP1);
  and and_1 (RegWSrc0, OP3, OP2);
  not not_13 (not_13_out, OP1);
  not not_14 (not_14_out, OP0);
  not not_15 (not_15_out, OP1);
  and and_2 (and_2_out, not_1_out, not_2_out, not_3_out);
  and and_3 (and_3_out, not_4_out, not_5_out, not_6_out);
  and and_4 (and_4_out, not_7_out, OP2);
  and and_5 (and_5_out, OP3, not_8_out);
  and and_6 (and_6_out, OP4, not_9_out, OP1);
  and and_7 (and_7_out, OP4, OP3, OP0);
  and and_8 (and_8_out, not_10_out, not_11_out, not_12_out);
  and and_9 (and_9_out, OP4, OP2);
  and and_10 (memoryRead, OP3, OP2, not_13_out, not_14_out);
  and and_11 (memoryWrite, OP3, OP2, not_15_out, OP0);
  or or_1 (RegWrite, and_2_out, and_3_out, and_4_out, and_5_out, and_6_out, and_7_out);
  or or_2 (RegDest0, and_8_out, and_9_out);

  assign RegDest1 = OP4;
  assign RegWSrc1 = OP4;
endmodule

module ProgramCounterControlUnit (
  input  OP4,
  input  OP3,
  input  OP2,
  input  OP1,
  input  OP0,
  output PCSrc0,
  output PCSrc1,
  output BrachOP0,
  output BranchOP1,
  output JumpOP
);

  wire and_1_out, and_2_out, and_3_out, and_4_out, and_5_out, and_6_out, and_7_out, not_1_out, not_2_out,
       not_3_out, not_4_out, not_5_out, not_6_out, not_7_out, not_8_out, not_11_out;

  not not_1 (not_1_out, OP4);
  not not_2 (not_2_out, OP2);
  not not_3 (not_3_out, OP3);
  not not_4 (not_4_out, OP4);
  not not_5 (not_5_out, OP3);
  not not_6 (not_6_out, OP4);
  not not_7 (not_7_out, OP1);
  not not_8 (not_8_out, OP2);
  not not_9 (BranchOP1, OP1);
  not not_10 (JumpOP, OP3);
  not not_11 (not_11_out, OP1);
  and and_1 (and_1_out, not_1_out, OP2);
  and and_2 (and_2_out, OP3, not_2_out);
  and and_3 (and_3_out, OP4, not_3_out);
  and and_4 (and_4_out, not_4_out, not_5_out);
  and and_5 (and_5_out, not_6_out, not_7_out);
  and and_6 (and_6_out, not_8_out, OP1);
  and and_7 (and_7_out, OP4, OP2);
  or or_1 (PCSrc0, not_11_out, and_1_out, and_2_out, and_3_out);
  or or_2 (PCSrc1, and_4_out, and_5_out, and_6_out, and_7_out);

  assign BrachOP0 = OP0;
endmodule
