// Logisim project JBControl.circ as structural Verilog
module JumpControl (
  input  [15:0] PC,
  input  [15:0] Rs,
  input  [10:0] Imm1,
  input  JOperation,
  output [15:0] newPC
);

  wire [15:0] adder_1_out, Imm;

  assign Imm = {{5{Imm1[10]}}, Imm1};  // Bit_Extender bit_extender_1
  Adder #(.width(16)) adder_1 (.a(PC), .b(Imm), .out(adder_1_out), .cin(1'b0));  // open: cout
  Multiplexer #(.width(16), .enable("false")) multiplexer_1 (
    .in0(adder_1_out), .in1(Rs), .out(newPC), .sel(JOperation));
endmodule

module BranchControl (
  input  [1:0] Operation,
  input  Zero,
  input  Less_Than,
  input  [4:0] Imm5,
  input  [15:0] PC,
  output [15:0] newPC
);

  wire not_1_out, not_2_out, not_3_out, not_4_out;
  wire [15:0] Beq, Bge, Blt, Bne, Imm16, PC_1, updatedPC;

  assign Imm16 = {{11{Imm5[4]}}, Imm5};  // Bit_Extender bit_extender_1
  assign Beq = not_1_out ? PC_1 : 16'bz;  // Controlled_Buffer controlled_buffer_1
  not not_1 (not_1_out, Zero);
  assign Beq = Zero ? updatedPC : 16'bz;  // Controlled_Buffer controlled_buffer_2
  assign Bne = not_2_out ? updatedPC : 16'bz;  // Controlled_Buffer controlled_buffer_3
  not not_2 (not_2_out, Zero);
  assign Bne = Zero ? PC_1 : 16'bz;  // Controlled_Buffer controlled_buffer_4
  not not_3 (not_3_out, Less_Than);
  not not_4 (not_4_out, Less_Than);
  Adder #(.width(16)) adder_1 (.a(PC), .b(Imm16), .out(updatedPC), .cin(1'b0));  // open: cout
  Adder #(.width(16)) adder_2 (.a(PC), .b({16{1'b0}}), .out(PC_1), .cin(1'b1));  // open: cout
  assign Blt = not_3_out ? PC_1 : 16'bz;  // Controlled_Buffer controlled_buffer_5
  assign Blt = Less_Than ? updatedPC : 16'bz;  // Controlled_Buffer controlled_buffer_6
  assign Bge = not_4_out ? updatedPC : 16'bz;  // Controlled_Buffer controlled_buffer_7
  assign Bge = Less_Than ? PC_1 : 16'bz;  // Controlled_Buffer controlled_buffer_8
  Multiplexer #(.select(2), .width(16), .enable("false")) multiplexer_1 (
    .in0(Beq), .in1(Bne), .in2(Blt), .in3(Bge), .out(newPC), .sel(Operation));

  // Other names for the same wires on the sheet: Less = Less_Than
endmodule
