// Logisim project file.circ as structural Verilog: 4 circuits, main circuit alu arithmetic
module alu_arithmetic (
  input  [1:0] Operation,
  input  [15:0] in_2,
  input  [15:0] in_3,
  output Zero,
  output Overflow,
  output [15:0] Output
);

  wire addersubtractor_1_carryout, addersubtractor_2_carryout, addersubtractor_3_carryout,
       addersubtractor_4_carryout, addersubtractor_5_carryout, addersubtractor_6_carryout,
       addersubtractor_7_carryout, addersubtractor_8_carryout, addersubtractor_9_carryout,
       addersubtractor_10_carryout, addersubtractor_11_carryout, addersubtractor_12_carryout,
       addersubtractor_13_carryout, addersubtractor_14_carryout, C14, C15, multiplexer_4_out, not_1_out,
       not_2_out, or_1_out, or_2_out, or_3_out, or_4_out, or_5_out, or_6_out, or_7_out, or_8_out, or_9_out,
       or_10_out, or_11_out, or_12_out, or_13_out, or_14_out, or_15_out, or_16_out, Set, SetUnsigned, Sub,
       xor_1_out, z0, z1, z2, z3, z4, z5, z6, z7, z8, z9, z10, z11, z12, z13, z14, z15;

  OperationDecoder operationdecoder_1 (.SUB(Sub), .SLT(Set), .SLTU(SetUnsigned), .Operation(Operation));
  AdderSubtractor addersubtractor_1 (
    .A(in_3[0]), .B(in_2[0]), .CarryIn(Sub), .BNegate(Sub), .CarryOut(addersubtractor_1_carryout), .Out(z0));
  AdderSubtractor addersubtractor_2 (
    .A(in_3[1]), .B(in_2[1]), .CarryIn(addersubtractor_1_carryout), .BNegate(Sub),
    .CarryOut(addersubtractor_2_carryout), .Out(z1));
  AdderSubtractor addersubtractor_3 (
    .A(in_3[2]), .B(in_2[2]), .CarryIn(addersubtractor_2_carryout), .BNegate(Sub),
    .CarryOut(addersubtractor_3_carryout), .Out(z2));
  AdderSubtractor addersubtractor_4 (
    .A(in_3[3]), .B(in_2[3]), .CarryIn(addersubtractor_3_carryout), .BNegate(Sub),
    .CarryOut(addersubtractor_4_carryout), .Out(z3));
  AdderSubtractor addersubtractor_5 (
    .A(in_3[4]), .B(in_2[4]), .CarryIn(addersubtractor_4_carryout), .BNegate(Sub),
    .CarryOut(addersubtractor_5_carryout), .Out(z4));
  AdderSubtractor addersubtractor_6 (
    .A(in_3[5]), .B(in_2[5]), .CarryIn(addersubtractor_5_carryout), .BNegate(Sub),
    .CarryOut(addersubtractor_6_carryout), .Out(z5));
  AdderSubtractor addersubtractor_7 (
    .A(in_3[6]), .B(in_2[6]), .CarryIn(addersubtractor_6_carryout), .BNegate(Sub),
    .CarryOut(addersubtractor_7_carryout), .Out(z6));
  AdderSubtractor addersubtractor_8 (
    .A(in_3[7]), .B(in_2[7]), .CarryIn(addersubtractor_7_carryout), .BNegate(Sub),
    .CarryOut(addersubtractor_8_carryout), .Out(z7));
  AdderSubtractor addersubtractor_9 (
    .A(in_3[8]), .B(in_2[8]), .CarryIn(addersubtractor_8_carryout), .BNegate(Sub),
    .CarryOut(addersubtractor_9_carryout), .Out(z8));
  AdderSubtractor addersubtractor_10 (
    .A(in_3[9]), .B(in_2[9]), .CarryIn(addersubtractor_9_carryout), .BNegate(Sub),
    .CarryOut(addersubtractor_10_carryout), .Out(z9));
  AdderSubtractor addersubtractor_11 (
    .A(in_3[10]), .B(in_2[10]), .CarryIn(addersubtractor_10_carryout), .BNegate(Sub),
    .CarryOut(addersubtractor_11_carryout), .Out(z10));
  AdderSubtractor addersubtractor_12 (
    .A(in_3[11]), .B(in_2[11]), .CarryIn(addersubtractor_11_carryout), .BNegate(Sub),
    .CarryOut(addersubtractor_12_carryout), .Out(z11));
  AdderSubtractor addersubtractor_13 (
    .A(in_3[12]), .B(in_2[12]), .CarryIn(addersubtractor_12_carryout), .BNegate(Sub),
    .CarryOut(addersubtractor_13_carryout), .Out(z12));
  AdderSubtractor addersubtractor_14 (
    .A(in_3[13]), .B(in_2[13]), .CarryIn(addersubtractor_13_carryout), .BNegate(Sub),
    .CarryOut(addersubtractor_14_carryout), .Out(z13));
  AdderSubtractor addersubtractor_15 (
    .A(in_3[14]), .B(in_2[14]), .CarryIn(addersubtractor_14_carryout), .BNegate(Sub), .CarryOut(C14),
    .Out(z14));
  AdderSubtractor addersubtractor_16 (
    .A(in_3[15]), .B(in_2[15]), .CarryIn(C14), .BNegate(Sub), .CarryOut(C15), .Out(z15));
  not not_1 (not_1_out, C15);
  xor xor_1 (xor_1_out, z15, Overflow);
  Multiplexer #(.enable("false")) multiplexer_1 (.in0(z1), .in1(1'b0), .out(Output[1]), .sel(or_1_out));
  or or_1 (or_1_out, SetUnsigned, Set);
  Multiplexer #(.enable("false")) multiplexer_2 (.in0(z3), .in1(1'b0), .out(Output[3]), .sel(or_2_out));
  or or_2 (or_2_out, SetUnsigned, Set);
  Multiplexer #(.enable("false")) multiplexer_3 (.in0(z5), .in1(1'b0), .out(Output[5]), .sel(or_3_out));
  or or_3 (or_3_out, SetUnsigned, Set);
  or or_4 (or_4_out, SetUnsigned, Set);
  or or_5 (or_5_out, SetUnsigned, Set);
  or or_6 (or_6_out, SetUnsigned, Set);
  xor xor_2 (Overflow, C14, C15);
  Multiplexer #(.enable("false")) multiplexer_4 (
    .in0(not_1_out), .in1(xor_1_out), .out(multiplexer_4_out), .sel(not_2_out));
  not not_2 (not_2_out, SetUnsigned);
  Multiplexer #(.enable("false")) multiplexer_5 (.in0(z7), .in1(1'b0), .out(Output[7]), .sel(or_4_out));
  Multiplexer #(.enable("false")) multiplexer_6 (.in0(z9), .in1(1'b0), .out(Output[9]), .sel(or_5_out));
  Multiplexer #(.enable("false")) multiplexer_7 (.in0(z11), .in1(1'b0), .out(Output[11]), .sel(or_6_out));
  Multiplexer #(.enable("false")) multiplexer_8 (.in0(z13), .in1(1'b0), .out(Output[13]), .sel(or_7_out));
  or or_7 (or_7_out, SetUnsigned, Set);
  or or_8 (or_8_out, SetUnsigned, Set);
  Multiplexer #(.enable("false")) multiplexer_9 (.in0(z2), .in1(1'b0), .out(Output[2]), .sel(or_9_out));
  or or_9 (or_9_out, SetUnsigned, Set);
  Multiplexer #(.enable("false")) multiplexer_10 (.in0(z4), .in1(1'b0), .out(Output[4]), .sel(or_10_out));
  or or_10 (or_10_out, SetUnsigned, Set);
  Multiplexer #(.enable("false")) multiplexer_11 (.in0(z6), .in1(1'b0), .out(Output[6]), .sel(or_11_out));
  or or_11 (or_11_out, SetUnsigned, Set);
  Multiplexer #(.enable("false")) multiplexer_12 (.in0(z8), .in1(1'b0), .out(Output[8]), .sel(or_12_out));
  or or_12 (or_12_out, SetUnsigned, Set);
  Multiplexer #(.enable("false")) multiplexer_13 (.in0(z10), .in1(1'b0), .out(Output[10]), .sel(or_13_out));
  or or_13 (or_13_out, SetUnsigned, Set);
  or or_14 (or_14_out, SetUnsigned, Set);
  or or_15 (or_15_out, SetUnsigned, Set);
  Multiplexer #(.enable("false")) multiplexer_14 (.in0(z15), .in1(1'b0), .out(Output[15]), .sel(or_16_out));
  or or_16 (or_16_out, SetUnsigned, Set);
  Multiplexer #(.enable("false")) multiplexer_15 (.in0(z0), .in1(multiplexer_4_out), .out(Output[0]), .sel(or_8_out));
  Multiplexer #(.enable("false")) multiplexer_16 (.in0(z12), .in1(1'b0), .out(Output[12]), .sel(or_14_out));
  Multiplexer #(.enable("false")) multiplexer_17 (.in0(z14), .in1(1'b0), .out(Output[14]), .sel(or_15_out));
  nor nor_1 (Zero, z0, z1, z2, z3, z4, z5, z6, z7, z8, z15, z14, z13, z12, z11, z10, z9);

  // Other names for the same wires on the sheet: b0 = in_2[0]; b1 = in_2[1]; b2 = in_2[2]; b3 = in_2[3]; b4 = in_2[4];
  //   b5 = in_2[5]; b6 = in_2[6]; b7 = in_2[7]; b8 = in_2[8]; b9 = in_2[9]; b10 = in_2[10]; b11 = in_2[11];
  //   b12 = in_2[12]; b13 = in_2[13]; b14 = in_2[14]; b15 = in_2[15]; a0 = in_3[0]; a1 = in_3[1]; a2 = in_3[2];
  //   a3 = in_3[3]; a4 = in_3[4]; a5 = in_3[5]; a6 = in_3[6]; a7 = in_3[7]; a8 = in_3[8]; a9 = in_3[9];
  //   a10 = in_3[10]; a11 = in_3[11]; a12 = in_3[12]; a13 = in_3[13]; a14 = in_3[14]; a15 = in_3[15]; o0 = Output[0];
  //   o1 = Output[1]; o2 = Output[2]; o3 = Output[3]; o4 = Output[4]; o5 = Output[5]; o6 = Output[6]; o7 = Output[7];
  //   o8 = Output[8]; o9 = Output[9]; o10 = Output[10]; o11 = Output[11]; o12 = Output[12]; o13 = Output[13];
  //   o14 = Output[14]; o15 = Output[15]

  // Notes on the sheet:
  //   B
  //   A
endmodule

module AdderSubtractor (
  input  A,
  input  B,
  input  CarryIn,
  input  BNegate,
  output CarryOut,
  output Out
);

  wire ActualB, Bin;

  not not_1 (Bin, B);
  Multiplexer #(.enable("false")) multiplexer_1 (.in0(B), .in1(Bin), .out(ActualB), .sel(BNegate));
  Adder #(.width(1)) adder_1 (.a(A), .b(ActualB), .out(Out), .cin(CarryIn), .cout(CarryOut));

  // Other names for the same wires on the sheet: cin = CarryIn; cout = CarryOut
endmodule

module testBench (
  input  in_1,
  input  in_2,
  input  in_3
);

  wire button_1_out, clock_1_out;
  wire [6:0] counter_1_q;
  wire [15:0] ram_1_data, rom_1_data, rom_2_data;

  Counter #(.width(7), .max('h7f)) counter_1 (
    .count(1'b1), .Q(counter_1_q), .clk(clock_1_out));  // open: load, D, carry, clr
  Clock clock_1 (.out(clock_1_out));
  ROM #(.addrWidth(7), .dataWidth(16)) rom_1 (.addr(counter_1_q), .data(rom_1_data), .sel(1'b1));
  ROM #(.addrWidth(7), .dataWidth(16)) rom_2 (.addr(counter_1_q), .data(rom_2_data), .sel(1'b1));
  RAM #(.addrWidth(7), .dataWidth(16)) ram_1 (
    .addr(counter_1_q), .data(ram_1_data), .sel(1'b1), .clk(clock_1_out), .ld(1'b0), .clr(button_1_out));
  Button button_1 (.out(button_1_out));
  // Probe on ram_1_data
  // alu_arithmetic alu_arithmetic_1: pin names not known; wires that end beside it: rom_1_data, rom_2_data, in_1, in_2, in_3, ram_1_data

  // Notes on the sheet:
  //   contents of rom_1 (hex, n*v repeats v):
  //   8b49 71ed fe10 2af5 e9b1 47d9 fd98 e87 c987 e50d 56b2 ccfc 108e a2b4 5a9c 97ec 3cdb 8e8 34f 8141
  //   970f 18aa 7f4c d858 728f 1796 4510 2b54 bf35 7d9f 2674 d107 c21f 38de 81bb dc7e 536d fba1 18a7 2aeb
  //   f6f8 5fbf b3ad 39e 9dab fca1 9f30 7cc df50 e829 2dac 488e 3563 56fb e938 438c 32dc 247a be2a 3177
  //   19bb 2afa 5287 8305 a7f9 fc3a 2a9b 727e c7de 82a2 55e7 4e71 9663 7aac 8010 28d4 73cd 5a1c b87e f5d7
  //   3187 2a56 b698 c54a 5c29 e1ce 1ac 11e6 9524 f413 107a d98a d7a0 1418 95be 8ca0 4c9a 354c 42a4 7d65
  //   5186 3e27 fd48 86fc b3a9 acc6 3e39 7327 4027 d27c 96bd 1cc ed21 4e8f e989 8eb8 4b91 7c92 bc84 acb3
  //   576a 7a2b ebc7 f2d0 499e d86d 1b92 60bd
  //   contents of rom_2 (hex, n*v repeats v):
  //   3faf e7b4 a42a bb00 1e2f a408 a9ad 1c74 ef2e b009 e818 648b 6272 291b 7912 6b29 558d e173 7ba ea8e
  //   b30b 282e 90bc dcba 25ff 8503 3aa4 23a1 26a4 fb07 cf9f 327c 79e6 16e1 cd5c 9f53 d7ce 277f 779 f836
  //   82f8 d4f5 27d3 39d0 3e7b b794 7c93 23e0 3f17 b5cf 1468 dd5d 54c dbd 8f7b 414c 895e ae5f 7cda 3d1e
  //   3147 a7df 4f4 e351 9253 8125 a457 3964 c0e b6a6 45a3 d3c6 cfbe ee14 ad6f e211 5d82 d3ba 3118 8fb6
  //   f611 37f0 38b2 45c1 3daa d4cb f672 e101 455a 7dab 4cba f844 b219 864e 7a57 f7fa 5617 60aa 9c78 edd1
  //   7396 d329 2cb3 7c8e c36b d953 992c 1331 4b43 56d0 a4f1 50f5 8e1f cb3b 4481 3393 d117 65fa 3d21 6f64
  //   fa12 cd0d f092 c9f1 52c2 fd5f 5fc7 b3ea
endmodule

module OperationDecoder (
  input  [1:0] Operation,
  output SUB,
  output SLT,
  output SLTU
);

  wire not_1_out;

  not not_1 (not_1_out, Operation[0]);
  or or_1 (SUB, Operation[0], Operation[1]);
  and and_1 (SLT, Operation[1], not_1_out);
  and and_2 (SLTU, Operation[1], Operation[0]);
endmodule
