// Logisim project BranchPrediction.circ as structural Verilog: 4 circuits, main circuit StateRegisters
module StateRegisters (
  input  [2:0] Read_Address,
  input  [2:0] Write_Address,
  input  [1:0] New_State,
  input  in_4,
  output [1:0] currentState
);

  wire S1, S2, S3, S4, S5, S6, S7, S8;
  wire [1:0] R1, R2, R3, R4, R5, R6, R7, R8;

  Register #(.width(2)) register_1 (.D(New_State), .en(S1), .Q(R1), .clk(in_4));  // open: clr
  Register #(.width(2)) register_2 (.D(New_State), .en(S5), .Q(R5), .clk(in_4));  // open: clr
  Register #(.width(2)) register_3 (.D(New_State), .en(S6), .Q(R6), .clk(in_4));  // open: clr
  Register #(.width(2)) register_4 (.D(New_State), .en(S2), .Q(R2), .clk(in_4));  // open: clr
  RegisterSelector registerselector_1 (
    .Register_S(Read_Address), .R1(R1), .R2(R2), .R3(R3), .R4(R4), .R5(R5), .R6(R6), .R7(R7),
    .out_10(currentState), .R8(R8));
  Register #(.width(2)) register_5 (.D(New_State), .en(S3), .Q(R3), .clk(in_4));  // open: clr
  Register #(.width(2)) register_6 (.D(New_State), .en(S7), .Q(R7), .clk(in_4));  // open: clr
  Register #(.width(2)) register_7 (.D(New_State), .en(S4), .Q(R4), .clk(in_4));  // open: clr
  Register #(.width(2)) register_8 (.D(New_State), .en(S8), .Q(R8), .clk(in_4));  // open: clr
  Decoder #(.select(3), .enable("false")) decoder_1 (
    .out0(S1), .out1(S2), .out2(S3), .out3(S4), .out4(S5), .out5(S6), .out6(S7), .out7(S8),
    .sel(Write_Address));

  // Other names for the same wires on the sheet: CLK = in_4; newState[1:0] = New_State;
  //   ReadAddress[2:0] = Read_Address; WriteAddress[2:0] = Write_Address
endmodule

module PredefinedAddressRegisters (
  input  in_1,
  input  [2:0] Read_Address,
  input  [2:0] Write_Address,
  input  [15:0] newAddress,
  output [15:0] currentAddress
);

  wire S1, S2, S3, S4, S5, S6, S7, S8;
  wire [15:0] R1, R2, R3, R4, R5, R6, R7, R8;

  Register #(.width(16)) register_1 (.D(newAddress), .en(S1), .Q(R1), .clk(in_1));  // open: clr
  Register #(.width(16)) register_2 (.D(newAddress), .en(S5), .Q(R5), .clk(in_1));  // open: clr
  Register #(.width(16)) register_3 (.D(newAddress), .en(S2), .Q(R2), .clk(in_1));  // open: clr
  Register #(.width(16)) register_4 (.D(newAddress), .en(S6), .Q(R6), .clk(in_1));  // open: clr
  RegisterSelector registerselector_1 (
    .Register_S(Read_Address), .R1(R1), .R2(R2), .R3(R3), .R4(R4), .R5(R5), .R6(R6), .R7(R7),
    .out_10(currentAddress), .R8(R8));
  Register #(.width(16)) register_5 (.D(newAddress), .en(S3), .Q(R3), .clk(in_1));  // open: clr
  Register #(.width(16)) register_6 (.D(newAddress), .en(S7), .Q(R7), .clk(in_1));  // open: clr
  Register #(.width(16)) register_7 (.D(newAddress), .en(S4), .Q(R4), .clk(in_1));  // open: clr
  Register #(.width(16)) register_8 (.D(newAddress), .en(S8), .Q(R8), .clk(in_1));  // open: clr
  Decoder #(.select(3), .enable("false")) decoder_1 (
    .out0(S1), .out1(S2), .out2(S3), .out3(S4), .out4(S5), .out5(S6), .out6(S7), .out7(S8),
    .sel(Write_Address));

  // Other names for the same wires on the sheet: CLK = in_1; ReadAddress[2:0] = Read_Address;
  //   WriteAddress[2:0] = Write_Address
endmodule

module PredictionCircuit (
  input  [2:0] BranchAddress,
  input  [15:0] newPC,
  input  [15:0] InstructionAddress,
  input  Decode_BranchTaken,
  input  Decode_JumpTaken,
  input  in_6,
  input  enable,
  output [15:0] PredictedPC,
  output controlPC,
  output flush,
  output prevPrediction
);

  wire and_2_out, and_3_out, and_4_out, and_6_out, and_7_out, and_8_out, CLK, comparator_1_eq, enable_t,
       isStateThree, isStateZero, not_1_out, not_2_out, not_3_out, not_4_out, not_5_out, not_6_out,
       not_7_out, not_8_out, or_1_out, or_2_out, or_3_out, or_4_out;
  wire [1:0] adder_1_out, branchNotTakenState, branchTakenState, currentState, newState, prevState,
       subtractor_1_out;
  wire [2:0] prevBranchAddress;
  wire [15:0] currentInstructionAddress, multiplexer_1_out, multiplexer_2_out, prevInstructionAddress;

  and and_1 (CLK, in_6, enable);
  or or_1 (or_1_out, Decode_BranchTaken, Decode_JumpTaken);
  or or_2 (or_2_out, Decode_BranchTaken, Decode_JumpTaken);
  and and_2 (and_2_out, ~flush, controlPC);  // AND_Gate
  Multiplexer #(.width(16), .enable("false")) multiplexer_1 (
    .in0({16{1'b0}}), .in1(newPC), .out(multiplexer_1_out), .sel(or_1_out));
  Multiplexer #(.width(16), .enable("false")) multiplexer_2 (
    .in0({16{1'b0}}), .in1(prevInstructionAddress), .out(multiplexer_2_out), .sel(or_2_out));
  Register #(.width(2)) u_prevState (.D(currentState), .Q(prevState), .clk(CLK));  // open: en, clr
  Register #(.width(3)) u_prevBranchAddress (
    .D(BranchAddress), .en(enable_t), .Q(prevBranchAddress), .clk(CLK));  // open: clr
  Register #(.width(1)) u_prevPrediction (.D(and_2_out), .Q(prevPrediction), .clk(CLK));  // open: en, clr
  Register #(.width(16)) u_prevInstructionAddress (
    .D(InstructionAddress), .Q(prevInstructionAddress), .clk(CLK));  // open: en, clr
  StateRegisters stateregisters_1 (
    .Read_Address(BranchAddress), .Write_Address(prevBranchAddress), .New_State(newState),
    .currentState(currentState), .in_4(CLK));
  PredefinedAddressRegisters predefinedaddressregisters_1 (
    .in_1(CLK), .Read_Address(BranchAddress), .Write_Address(prevBranchAddress),
    .newAddress(multiplexer_1_out), .currentAddress(PredictedPC));
  AddressRegisters addressregisters_1 (
    .in_1(CLK), .Read_Address(BranchAddress), .Write_Address(prevBranchAddress),
    .newAddress(multiplexer_2_out), .currentAddress(currentInstructionAddress));
  not not_1 (not_1_out, currentState[0]);
  not not_2 (not_2_out, currentState[1]);
  not not_3 (not_3_out, currentState[1]);
  and and_3 (and_3_out, not_1_out, not_2_out);
  and and_4 (and_4_out, currentState[0], not_3_out);
  not not_4 (not_4_out, or_3_out);
  or or_3 (or_3_out, and_3_out, and_4_out);
  Comparator #(.width(16)) comparator_1 (
    .a(InstructionAddress), .b(currentInstructionAddress), .eq(comparator_1_eq));  // open: gt, lt
  Subtractor #(.width(2)) subtractor_1 (.a(prevState), .b(2'b01), .out(subtractor_1_out));  // open: bin, bout
  Adder #(.width(2)) adder_1 (.a(prevState), .b(2'b01), .out(adder_1_out));  // open: cin, cout
  nor nor_1 (isStateZero, prevState[0], prevState[1]);
  Multiplexer #(.width(2), .enable("false")) multiplexer_3 (
    .in0(subtractor_1_out), .in1(prevState), .out(branchNotTakenState), .sel(isStateZero));
  and and_5 (isStateThree, prevState[0], prevState[1]);
  Multiplexer #(.width(2), .enable("false")) multiplexer_4 (
    .in0(adder_1_out), .in1(prevState), .out(branchTakenState), .sel(isStateThree));
  assign newState = and_6_out ? 2'b11 : 2'bz;  // Controlled_Buffer controlled_buffer_1
  and and_6 (and_6_out, Decode_JumpTaken, not_5_out);
  not not_5 (not_5_out, Decode_BranchTaken);
  assign newState = and_7_out ? branchNotTakenState : 2'bz;  // Controlled_Buffer controlled_buffer_2
  and and_7 (and_7_out, not_6_out, not_7_out);
  not not_6 (not_6_out, Decode_JumpTaken);
  not not_7 (not_7_out, Decode_BranchTaken);
  assign newState = and_8_out ? branchTakenState : 2'bz;  // Controlled_Buffer controlled_buffer_3
  and and_8 (and_8_out, not_8_out, Decode_BranchTaken);
  not not_8 (not_8_out, Decode_JumpTaken);
  or or_4 (or_4_out, Decode_BranchTaken, Decode_JumpTaken);
  and and_9 (controlPC, not_4_out, comparator_1_eq);
  xor xor_1 (flush, or_4_out, prevPrediction);
endmodule

module AddressRegisters (
  input  in_1,
  input  [2:0] Read_Address,
  input  [2:0] Write_Address,
  input  [15:0] newAddress,
  output [15:0] currentAddress
);

  wire S1, S2, S3, S4, S5, S6, S7, S8;
  wire [15:0] R1, R2, R3, R4, R5, R6, R7, R8;

  Register #(.width(16)) register_1 (.D(newAddress), .en(S1), .Q(R1), .clk(in_1));  // open: clr
  Register #(.width(16)) register_2 (.D(newAddress), .en(S5), .Q(R5), .clk(in_1));  // open: clr
  Register #(.width(16)) register_3 (.D(newAddress), .en(S2), .Q(R2), .clk(in_1));  // open: clr
  Register #(.width(16)) register_4 (.D(newAddress), .en(S6), .Q(R6), .clk(in_1));  // open: clr
  RegisterSelector registerselector_1 (
    .Register_S(Read_Address), .R1(R1), .R2(R2), .R3(R3), .R4(R4), .R5(R5), .R6(R6), .R7(R7),
    .out_10(currentAddress), .R8(R8));
  Register #(.width(16)) register_5 (.D(newAddress), .en(S3), .Q(R3), .clk(in_1));  // open: clr
  Register #(.width(16)) register_6 (.D(newAddress), .en(S7), .Q(R7), .clk(in_1));  // open: clr
  Register #(.width(16)) register_7 (.D(newAddress), .en(S4), .Q(R4), .clk(in_1));  // open: clr
  Register #(.width(16)) register_8 (.D(newAddress), .en(S8), .Q(R8), .clk(in_1));  // open: clr
  Decoder #(.select(3), .enable("false")) decoder_1 (
    .out0(S1), .out1(S2), .out2(S3), .out3(S4), .out4(S5), .out5(S6), .out6(S7), .out7(S8),
    .sel(Write_Address));

  // Other names for the same wires on the sheet: CLK = in_1; ReadAddress[2:0] = Read_Address;
  //   WriteAddress[2:0] = Write_Address
endmodule
