// Logisim project PredefinedAddressRegisterSelector.circ as structural Verilog: 1 circuit, main circuit RegisterSelector
module RegisterSelector (
  input  [2:0] Register_S,
  input  [15:0] R1,
  input  [15:0] R2,
  input  [15:0] R3,
  input  [15:0] R4,
  input  [15:0] R5,
  input  [15:0] R6,
  input  [15:0] R7,
  input  [15:0] R8,
  output [15:0] out_10
);

  wire S0, S1, S2, S3, S4, S5, S6, S7;

  assign out_10 = S0 ? R1 : 16'bz;  // Controlled_Buffer controlled_buffer_1
  assign out_10 = S1 ? R2 : 16'bz;  // Controlled_Buffer controlled_buffer_2
  assign out_10 = S2 ? R3 : 16'bz;  // Controlled_Buffer controlled_buffer_3
  assign out_10 = S3 ? R4 : 16'bz;  // Controlled_Buffer controlled_buffer_4
  assign out_10 = S4 ? R5 : 16'bz;  // Controlled_Buffer controlled_buffer_5
  assign out_10 = S5 ? R6 : 16'bz;  // Controlled_Buffer controlled_buffer_6
  assign out_10 = S6 ? R7 : 16'bz;  // Controlled_Buffer controlled_buffer_7
  assign out_10 = S7 ? R8 : 16'bz;  // Controlled_Buffer controlled_buffer_8
  Decoder #(.select(3), .enable("false")) decoder_1 (
    .out0(S0), .out1(S1), .out2(S2), .out3(S3), .out4(S4), .out5(S5), .out6(S6), .out7(S7), .sel(Register_S));

  // Other names for the same wires on the sheet: Register_R[15:0] = out_10
endmodule
