// Logisim project ControlUnitC.circ as structural Verilog: 4 circuits, main circuit ControlUnit
module ControlUnit (
  input  [4:0] Opcode,
  input  [1:0] Function,
  output [3:0] ALUop,
  output ALUSrc,
  output signExtend,
  output RegWrite,
  output [1:0] RegDest,
  output [1:0] RegWSrc,
  output memoryRead,
  output memoryWrite,
  output [1:0] PCSrc,
  output [1:0] BrachOP,
  output JumpOP
);

  ALUControlUnit alucontrolunit_1 (
    .OP4(Opcode[4]), .ALUop3(ALUop[3]), .OP3(Opcode[3]), .OP2(Opcode[2]), .OP1(Opcode[1]), .ALUop2(ALUop[2]),
    .OP0(Opcode[0]), .F1(Function[1]), .F0(Function[0]), .ALUop1(ALUop[1]), .ALUop0(ALUop[0]),
    .ALUSrc(ALUSrc), .signExtend(signExtend));
  RegistersMemoryControlUnit registersmemorycontrolunit_1 (
    .OP4(Opcode[4]), .OP3(Opcode[3]), .OP2(Opcode[2]), .OP1(Opcode[1]), .OP0(Opcode[0]), .RegWrite(RegWrite),
    .RegDest1(RegDest[1]), .RegDest0(RegDest[0]), .RegWSrc1(RegWSrc[1]), .RegWSrc0(RegWSrc[0]),
    .memoryRead(memoryRead), .memoryWrite(memoryWrite));
  ProgramCounterControlUnit programcountercontrolunit_1 (
    .OP4(Opcode[4]), .OP3(Opcode[3]), .PCSrc0(PCSrc[0]), .OP2(Opcode[2]), .OP1(Opcode[1]), .OP0(Opcode[0]),
    .PCSrc1(PCSrc[1]), .BrachOP0(BrachOP[0]), .BranchOP1(BrachOP[1]), .JumpOP(JumpOP));
endmodule

module ALUControlUnit (
  input  OP4,
  input  OP3,
  input  OP2,
  input  OP1,
  input  OP0,
  input  F1,
  input  F0,
  output ALUop3,
  output ALUop2,
  output ALUop1,
  output ALUop0,
  output ALUSrc,
  output signExtend
);

  wire and_2_out, and_3_out, and_4_out, and_5_out, and_6_out, and_7_out, and_8_out, and_9_out, and_10_out,
       and_11_out, and_12_out, and_13_out, and_14_out, and_15_out, and_16_out, not_1_out, not_2_out,
       not_3_out, not_4_out, not_5_out, not_6_out, not_7_out, not_8_out, not_9_out, not_10_out, not_11_out,
       not_12_out, not_13_out, not_14_out, not_15_out, not_16_out, not_17_out, not_18_out, not_19_out;

  not not_1 (not_1_out, OP2);
  not not_2 (not_2_out, OP3);
  not not_3 (not_3_out, OP2);
  not not_4 (not_4_out, OP3);
  not not_5 (not_5_out, OP3);
  not not_6 (not_6_out, OP2);
  not not_7 (not_7_out, OP3);
  not not_8 (not_8_out, OP0);
  not not_9 (not_9_out, OP2);
  not not_10 (not_10_out, OP4);
  not not_11 (not_11_out, OP3);
  not not_12 (not_12_out, OP2);
  not not_13 (not_13_out, OP3);
  not not_14 (not_14_out, OP1);
  not not_15 (not_15_out, OP2);
  not not_16 (not_16_out, OP3);
  not not_17 (not_17_out, OP2);
  not not_18 (not_18_out, OP1);
  not not_19 (not_19_out, OP3);
  and and_1 (ALUop3, OP3, not_1_out);
  and and_2 (and_2_out, not_2_out, not_3_out, OP0);
  and and_3 (and_3_out, not_4_out, OP1, OP0);
  and and_4 (and_4_out, OP3, OP2);
  and and_5 (and_5_out, not_5_out, not_6_out, F1);
  and and_6 (and_6_out, not_7_out, OP1, not_8_out);
  and and_7 (and_7_out, not_9_out, OP1);
  and and_8 (and_8_out, not_10_out, not_11_out, not_12_out, F0);
  and and_9 (and_9_out, not_13_out, OP2, not_14_out, OP0);
  and and_10 (and_10_out, OP3, not_15_out, OP0);
  and and_11 (and_11_out, OP3, OP2, OP1);
  and and_12 (and_12_out, not_16_out, OP2);
  and and_13 (and_13_out, OP3, not_17_out);
  and and_14 (and_14_out, OP3, not_18_out);
  and and_15 (and_15_out, not_19_out, OP1, OP0);
  and and_16 (and_16_out, OP3, OP2);
  or or_1 (ALUop2, and_2_out, and_3_out, and_4_out, OP4);
  or or_2 (ALUop1, and_5_out, and_6_out, and_7_out, OP4);
  or or_3 (ALUop0, and_8_out, and_9_out, and_10_out, and_11_out);
  or or_4 (ALUSrc, and_12_out, and_13_out, and_14_out);
  or or_5 (signExtend, and_15_out, and_16_out);
endmodule

module RegistersMemoryControlUnit (
  input  OP4,
  input  OP3,
  input  OP2,
  input  OP1,
  input  OP0,
  output RegWrite,
  output RegDest1,
  output RegDest0,
  output RegWSrc1,
  output RegWSrc0,
  output memoryRead,
  output memoryWrite
);

  wire and_1_out, and_2_out, and_3_out, and_4_out, and_5_out, and_6_out, and_7_out, and_8_out, and_9_out,
       and_10_out, and_11_out, not_1_out, not_2_out, not_3_out, not_4_out, not_5_out, not_6_out, not_7_out,
       not_8_out, not_9_out, not_10_out, not_11_out, not_12_out, not_13_out, not_14_out, not_15_out,
       not_16_out, not_17_out, not_18_out, not_19_out;

  not not_1 (not_1_out, OP4);
  not not_2 (not_2_out, OP3);
  not not_3 (not_3_out, OP1);
  not not_4 (not_4_out, OP4);
  not not_5 (not_5_out, OP1);
  not not_6 (not_6_out, OP0);
  not not_7 (not_7_out, OP3);
  not not_8 (not_8_out, OP2);
  not not_9 (not_9_out, OP3);
  not not_10 (not_10_out, OP0);
  not not_11 (not_11_out, OP3);
  not not_12 (not_12_out, OP2);
  not not_13 (not_13_out, OP1);
  not not_14 (not_14_out, OP3);
  not not_15 (not_15_out, OP3);
  not not_16 (not_16_out, OP2);
  not not_17 (not_17_out, OP1);
  not not_18 (not_18_out, OP0);
  not not_19 (not_19_out, OP1);
  and and_1 (and_1_out, not_1_out, not_2_out, not_3_out);
  and and_2 (and_2_out, not_4_out, not_5_out, not_6_out);
  and and_3 (and_3_out, not_7_out, OP2);
  and and_4 (and_4_out, OP3, not_8_out);
  and and_5 (and_5_out, OP4, not_9_out, OP1, not_10_out);
  and and_6 (and_6_out, OP4, OP3, OP0);
  and and_7 (and_7_out, not_11_out, not_12_out, not_13_out);
  and and_8 (and_8_out, OP4, not_14_out, OP0);
  and and_9 (and_9_out, OP4, OP2);
  and and_10 (and_10_out, OP3, OP2);
  and and_11 (and_11_out, OP4, not_15_out, not_16_out, OP1, OP0);
  and and_12 (memoryRead, OP3, OP2, not_17_out, not_18_out);
  and and_13 (memoryWrite, OP3, OP2, not_19_out, OP0);
  or or_1 (RegWrite, and_1_out, and_2_out, and_3_out, and_4_out, and_5_out, and_6_out);
  or or_2 (RegDest0, and_7_out, and_8_out, and_9_out);
  or or_3 (RegWSrc0, and_10_out, and_11_out);

  assign RegDest1 = OP4;
  assign RegWSrc1 = OP4;
endmodule

module ProgramCounterControlUnit (
  input  OP4,
  input  OP3,
  input  OP2,
  input  OP1,
  input  OP0,
  output PCSrc0,
  output PCSrc1,
  output BrachOP0,
  output BranchOP1,
  output JumpOP
);

  wire and_1_out, and_2_out, and_3_out, and_4_out, and_5_out, and_6_out, and_7_out, not_1_out, not_2_out,
       not_3_out, not_4_out, not_5_out, not_6_out, not_7_out, not_8_out, not_11_out;

  not not_1 (not_1_out, OP4);
  not not_2 (not_2_out, OP2);
  not not_3 (not_3_out, OP3);
  not not_4 (not_4_out, OP4);
  not not_5 (not_5_out, OP3);
  not not_6 (not_6_out, OP4);
  not not_7 (not_7_out, OP1);
  not not_8 (not_8_out, OP2);
  not not_9 (BranchOP1, OP1);
  not not_10 (JumpOP, OP3);
  not not_11 (not_11_out, OP1);
  and and_1 (and_1_out, not_1_out, OP2);
  and and_2 (and_2_out, OP3, not_2_out);
  and and_3 (and_3_out, OP4, not_3_out);
  and and_4 (and_4_out, not_4_out, not_5_out);
  and and_5 (and_5_out, not_6_out, not_7_out);
  and and_6 (and_6_out, not_8_out, OP1);
  and and_7 (and_7_out, OP4, OP2);
  or or_1 (PCSrc0, not_11_out, and_1_out, and_2_out, and_3_out);
  or or_2 (PCSrc1, and_4_out, and_5_out, and_6_out, and_7_out);

  assign BrachOP0 = OP0;
endmodule
