// Logisim project GPUC.circ as structural Verilog: 2 circuits, main circuit GPU
module GPU (
  input  [3:0] Column,
  input  en,
  input  [15:0] Data,
  input  clk,
  output [15:0] out_5,
  output [15:0] out_6,
  output [15:0] out_7,
  output [15:0] out_8,
  output [15:0] out_9,
  output [15:0] out_10,
  output [15:0] out_11,
  output [15:0] out_12,
  output [15:0] out_13,
  output [15:0] out_14,
  output [15:0] out_15,
  output [15:0] out_16,
  output [15:0] out_17,
  output [15:0] out_18,
  output [15:0] out_19,
  output [15:0] out_20
);

  wire c0, c1, c2, c3, c4, c5, c6, c7, c8, c9, c10, c11, c12, c13, c14, c15, decoder_1_out0, decoder_1_out1,
       decoder_1_out2, decoder_1_out3, decoder_1_out4, decoder_1_out5, decoder_1_out6, decoder_1_out7,
       decoder_1_out8, decoder_1_out9, decoder_1_out10, decoder_1_out11, decoder_1_out12, decoder_1_out13,
       decoder_1_out14, decoder_1_out15;

  Register #(.width(16)) register_1 (.D(Data), .en(c0), .Q(out_5), .clk(clk));  // open: clr
  Register #(.width(16)) register_2 (.D(Data), .en(c4), .Q(out_9), .clk(clk));  // open: clr
  Register #(.width(16)) register_3 (.D(Data), .en(c8), .Q(out_13), .clk(clk));  // open: clr
  Register #(.width(16)) register_4 (.D(Data), .en(c12), .Q(out_17), .clk(clk));  // open: clr
  Register #(.width(16)) register_5 (.D(Data), .en(c1), .Q(out_6), .clk(clk));  // open: clr
  Register #(.width(16)) register_6 (.D(Data), .en(c5), .Q(out_10), .clk(clk));  // open: clr
  Register #(.width(16)) register_7 (.D(Data), .en(c9), .Q(out_14), .clk(clk));  // open: clr
  Register #(.width(16)) register_8 (.D(Data), .en(c13), .Q(out_18), .clk(clk));  // open: clr
  Register #(.width(16)) register_9 (.D(Data), .en(c2), .Q(out_7), .clk(clk));  // open: clr
  Register #(.width(16)) register_10 (.D(Data), .en(c6), .Q(out_11), .clk(clk));  // open: clr
  Register #(.width(16)) register_11 (.D(Data), .en(c10), .Q(out_15), .clk(clk));  // open: clr
  Register #(.width(16)) register_12 (.D(Data), .en(c14), .Q(out_19), .clk(clk));  // open: clr
  Register #(.width(16)) register_13 (.D(Data), .en(c7), .Q(out_12), .clk(clk));  // open: clr
  Register #(.width(16)) register_14 (.D(Data), .en(c11), .Q(out_16), .clk(clk));  // open: clr
  Register #(.width(16)) register_15 (.D(Data), .en(c15), .Q(out_20), .clk(clk));  // open: clr
  Register #(.width(16)) register_16 (.D(Data), .en(c3), .Q(out_8), .clk(clk));  // open: clr
  Decoder #(.select(4), .enable("false")) decoder_1 (
    .out0(decoder_1_out0), .out1(decoder_1_out1), .out2(decoder_1_out2), .out3(decoder_1_out3),
    .out4(decoder_1_out4), .out5(decoder_1_out5), .out6(decoder_1_out6), .out7(decoder_1_out7),
    .out8(decoder_1_out8), .out9(decoder_1_out9), .out10(decoder_1_out10), .out11(decoder_1_out11),
    .out12(decoder_1_out12), .out13(decoder_1_out13), .out14(decoder_1_out14), .out15(decoder_1_out15),
    .sel(Column));
  and and_1 (c0, en, decoder_1_out0);
  and and_2 (c1, en, decoder_1_out1);
  and and_3 (c2, en, decoder_1_out2);
  and and_4 (c3, en, decoder_1_out3);
  and and_5 (c4, en, decoder_1_out4);
  and and_6 (c5, en, decoder_1_out5);
  and and_7 (c6, en, decoder_1_out6);
  and and_8 (c7, en, decoder_1_out7);
  and and_9 (c8, en, decoder_1_out8);
  and and_10 (c9, en, decoder_1_out9);
  and and_11 (c10, en, decoder_1_out10);
  and and_12 (c11, en, decoder_1_out11);
  and and_13 (c12, en, decoder_1_out12);
  and and_14 (c13, en, decoder_1_out13);
  and and_15 (c14, en, decoder_1_out14);
  and and_16 (c15, en, decoder_1_out15);

  // Other names for the same wires on the sheet: o0[15:0] = out_5; o1[15:0] = out_6; o2[15:0] = out_7;
  //   o3[15:0] = out_8; o4[15:0] = out_9; o5[15:0] = out_10; o6[15:0] = out_11; o7[15:0] = out_12; o8[15:0] = out_13;
  //   o9[15:0] = out_14; o10[15:0] = out_15; o11[15:0] = out_16; o12[15:0] = out_17; o13[15:0] = out_18;
  //   o14[15:0] = out_19; o15[15:0] = out_20
endmodule

module GPUcontrol (
  input  OP4,
  input  OP3,
  input  OP2,
  input  OP1,
  input  OP0,
  output En
);

  wire not_1_out, not_2_out;

  not not_1 (not_1_out, OP3);
  not not_2 (not_2_out, OP2);
  and and_1 (En, OP4, not_1_out, not_2_out, OP1, OP0);
endmodule
