// Logisim project JBControl.circ as structural Verilog
module JumpControl (
  input  [15:0] PC,
  input  [15:0] Rs,
  input  [10:0] Imm1,
  input  JOperation,
  input  [1:0] PCSrc,
  output [15:0] newPC,
  output JumpTaken
);

  wire not_1_out;
  wire [15:0] adder_1_out, Imm;

  assign Imm = {{5{Imm1[10]}}, Imm1};  // Bit_Extender bit_extender_1
  not not_1 (not_1_out, PCSrc[0]);
  Adder #(.width(16)) adder_1 (.a(PC), .b(Imm), .out(adder_1_out), .cin(1'b0));  // open: cout
  and and_1 (JumpTaken, not_1_out, PCSrc[1]);
  Multiplexer #(.width(16), .enable("false")) multiplexer_1 (
    .in0(adder_1_out), .in1(Rs), .out(newPC), .sel(JOperation));
endmodule

module BranchControl (
  input  [1:0] Operation,
  input  [15:0] A,
  input  [15:0] B,
  input  [4:0] Imm5,
  input  [15:0] PC,
  input  [1:0] PCSrc,
  output [15:0] newPC,
  output BranchTaken
);

  wire and_1_out, Equal, Less, multiplexer_2_out, not_1_out, not_2_out, not_3_out, not_4_out, not_5_out;
  wire [15:0] Beq, Bge, Blt, Bne, Imm16, updatedPC;

  assign Imm16 = {{11{Imm5[4]}}, Imm5};  // Bit_Extender bit_extender_1
  Comparator #(.width(16)) comparator_1 (.a(A), .b(B), .eq(Equal));  // open: gt, lt
  Comparator #(.width(16)) comparator_2 (.a(A), .b(B), .lt(Less));  // open: gt, eq
  Adder #(.width(16)) adder_1 (.a(PC), .b(Imm16), .out(updatedPC), .cin(1'b0));  // open: cout
  assign Beq = Equal ? updatedPC : 16'bz;  // Controlled_Buffer controlled_buffer_1
  assign Bne = not_1_out ? updatedPC : 16'bz;  // Controlled_Buffer controlled_buffer_2
  not not_1 (not_1_out, Equal);
  assign Blt = Less ? updatedPC : 16'bz;  // Controlled_Buffer controlled_buffer_3
  assign Bge = not_2_out ? updatedPC : 16'bz;  // Controlled_Buffer controlled_buffer_4
  not not_2 (not_2_out, Less);
  not not_3 (not_3_out, Less);
  not not_4 (not_4_out, Equal);
  not not_5 (not_5_out, PCSrc[1]);
  Multiplexer #(.select(2), .width(16), .enable("false")) multiplexer_1 (
    .in0(Beq), .in1(Bne), .in2(Blt), .in3(Bge), .out(newPC), .sel(Operation));
  Multiplexer #(.select(2), .enable("false")) multiplexer_2 (
    .in0(Equal), .in1(not_4_out), .in2(Less), .in3(not_3_out), .out(multiplexer_2_out), .sel(Operation));
  and and_1 (and_1_out, PCSrc[0], not_5_out);
  and and_2 (BranchTaken, multiplexer_2_out, and_1_out);
endmodule
