// Logisim project DataMemory.circ as structural Verilog: 1 circuit, main circuit Data Memory
module Data_Memory (
  input  CLK,
  input  Memory_Enable,
  input  Memory_Read,
  input  Memory_Write,
  input  [15:0] Address,
  input  [15:0] Data_In,
  output [15:0] Data_Out
);

  RAM #(.addrWidth(16), .dataWidth(16), .bus("separate")) ram_1 (
    .addr(Address), .din(Data_In), .data(Data_Out), .str(Memory_Write), .sel(Memory_Enable), .clk(CLK),
    .ld(Memory_Read));  // open: clr
endmodule
