// Logisim project FRU.circ as structural Verilog: 1 circuit, main circuit FRU
module FRU (
  input  CLK,
  input  RegWrite,
  input  RegEn,
  input  [15:0] BusW,
  output [15:0] BusR
);

  wire and_1_out;

  and and_1 (and_1_out, RegWrite, RegEn);
  Register #(.width(16)) register_1 (.D(BusW), .en(and_1_out), .Q(BusR), .clk(CLK), .clr(1'b0));
endmodule
