// Logisim project InstructionSplitterC.circ as structural Verilog: 1 circuit, main circuit InstructionSplitter
module InstructionSplitter (
  input  [15:0] Instruction,
  output [4:0] Op,
  output [1:0] F,
  output [2:0] Rd,
  output [2:0] Rs,
  output [2:0] Rt,
  output [4:0] Imm5,
  output [10:0] Imm11
);


  assign F = Instruction[10:9];
  assign Imm5 = Instruction[10:6];
  assign Imm11 = Instruction[10:0];
  assign Op = Instruction[15:11];
  assign Rd = Instruction[8:6];
  assign Rs = Instruction[5:3];
  assign Rt = Instruction[2:0];
endmodule
