// Logisim project FRU.circ as structural Verilog: 1 circuit, main circuit FRU
module FRU (
  input  CLK,
  input  RegWrite,
  input  RegEn,
  input  [31:0] BusW,
  output [31:0] BusR
);

  wire and_1_out;

  Register #(.width(32)) register_1 (.D(BusW), .en(and_1_out), .clk(CLK), .Q(BusR), .clr(1'b0));
  and and_1 (and_1_out, RegWrite, RegEn);
endmodule
