// Logisim project RegisterFileC.circ as structural Verilog: 1 circuit, main circuit RegisterFile
module RegisterFile (
  input  Reg_Write,
  input  CLK,
  input  [4:0] RA,
  input  [4:0] RB,
  input  [4:0] RW,
  input  [31:0] Bus_W,
  output [31:0] Bus_A,
  output [31:0] Bus_B
);

  wire S1, S2, S3, S4, S5, S6, S7, S8, S9, S10, S11, S12, S13, S14, S15, S16, S17, S18, S19, S20, S21, S22,
       S23, S24, S25, S26, S27, S28, S29, S30, S31;
  wire [31:0] R1, R2, R3, R4, R5, R6, R7, R8, R9, R10, R11, R12, R13, R14, R15, R16, R17, R18, R19, R20, R21,
       R22, R23, R24, R25, R26, R27, R28, R29, R30, R31;

  Decoder #(.enable("false"), .select(5)) decoder_1 (
    .out1(S1), .out2(S2), .out3(S3), .out4(S4), .out5(S5), .out6(S6), .out7(S7), .out8(S8), .out9(S9),
    .out10(S10), .out11(S11), .out12(S12), .out13(S13), .out14(S14), .out15(S15), .out16(S16), .out17(S17),
    .out18(S18), .out19(S19), .out20(S20), .out21(S21), .out22(S22), .out23(S23), .out24(S24), .out25(S25),
    .out26(S26), .out27(S27), .out28(S28), .out29(S29), .out30(S30), .out31(S31), .sel(RW));  // open: out0
  FRU fru_1 (.CLK(CLK), .RegWrite(Reg_Write), .RegEn(S21), .BusW(Bus_W), .BusR(R21));
  FRU fru_2 (.CLK(CLK), .RegWrite(Reg_Write), .RegEn(S25), .BusW(Bus_W), .BusR(R25));
  FRU fru_3 (.CLK(CLK), .RegWrite(Reg_Write), .RegEn(S29), .BusW(Bus_W), .BusR(R29));
  FRU fru_4 (.CLK(CLK), .RegWrite(Reg_Write), .RegEn(S1), .BusW(Bus_W), .BusR(R1));
  FRU fru_5 (.CLK(CLK), .RegWrite(Reg_Write), .RegEn(S5), .BusW(Bus_W), .BusR(R5));
  FRU fru_6 (.CLK(CLK), .RegWrite(Reg_Write), .RegEn(S9), .BusW(Bus_W), .BusR(R9));
  FRU fru_7 (.CLK(CLK), .RegWrite(Reg_Write), .RegEn(S13), .BusW(Bus_W), .BusR(R13));
  FRU fru_8 (.CLK(CLK), .RegWrite(Reg_Write), .RegEn(S17), .BusW(Bus_W), .BusR(R17));
  FRU fru_9 (.CLK(CLK), .RegWrite(Reg_Write), .RegEn(S2), .BusW(Bus_W), .BusR(R2));
  FRU fru_10 (.CLK(CLK), .RegWrite(Reg_Write), .RegEn(S6), .BusW(Bus_W), .BusR(R6));
  FRU fru_11 (.CLK(CLK), .RegWrite(Reg_Write), .RegEn(S10), .BusW(Bus_W), .BusR(R10));
  FRU fru_12 (.CLK(CLK), .RegWrite(Reg_Write), .RegEn(S14), .BusW(Bus_W), .BusR(R14));
  FRU fru_13 (.CLK(CLK), .RegWrite(Reg_Write), .RegEn(S18), .BusW(Bus_W), .BusR(R18));
  FRU fru_14 (.CLK(CLK), .RegWrite(Reg_Write), .RegEn(S22), .BusW(Bus_W), .BusR(R22));
  FRU fru_15 (.CLK(CLK), .RegWrite(Reg_Write), .RegEn(S26), .BusW(Bus_W), .BusR(R26));
  FRU fru_16 (.CLK(CLK), .RegWrite(Reg_Write), .RegEn(S30), .BusW(Bus_W), .BusR(R30));
  FRU fru_17 (.CLK(CLK), .RegWrite(Reg_Write), .RegEn(S3), .BusW(Bus_W), .BusR(R3));
  FRU fru_18 (.CLK(CLK), .RegWrite(Reg_Write), .RegEn(S7), .BusW(Bus_W), .BusR(R7));
  FRU fru_19 (.CLK(CLK), .RegWrite(Reg_Write), .RegEn(S11), .BusW(Bus_W), .BusR(R11));
  FRU fru_20 (.CLK(CLK), .RegWrite(Reg_Write), .RegEn(S15), .BusW(Bus_W), .BusR(R15));
  FRU fru_21 (.CLK(CLK), .RegWrite(Reg_Write), .RegEn(S19), .BusW(Bus_W), .BusR(R19));
  FRU fru_22 (.CLK(CLK), .RegWrite(Reg_Write), .RegEn(S23), .BusW(Bus_W), .BusR(R23));
  FRU fru_23 (.CLK(CLK), .RegWrite(Reg_Write), .RegEn(S27), .BusW(Bus_W), .BusR(R27));
  FRU fru_24 (.CLK(CLK), .RegWrite(Reg_Write), .RegEn(S31), .BusW(Bus_W), .BusR(R31));
  RegisterSelector registerselector_1 (
    .Register_S(RA), .R1(R1), .R2(R2), .R3(R3), .R4(R4), .R5(R5), .R6(R6), .R7(R7), .R8(R8), .R9(R9),
    .R10(R10), .R11(R11), .R12(R12), .R13(R13), .R14(R14), .R15(R15), .R16(R16), .R17(R17), .R18(R18),
    .R19(R19), .R20(R20), .R21(R21), .R22(R22), .R23(R23), .R24(R24), .R25(R25), .R26(R26), .R27(R27),
    .R28(R28), .R29(R29), .R30(R30), .R31(R31), .out_33(Bus_A));
  FRU fru_25 (.CLK(CLK), .RegWrite(Reg_Write), .RegEn(S4), .BusW(Bus_W), .BusR(R4));
  FRU fru_26 (.CLK(CLK), .RegWrite(Reg_Write), .RegEn(S8), .BusW(Bus_W), .BusR(R8));
  FRU fru_27 (.CLK(CLK), .RegWrite(Reg_Write), .RegEn(S12), .BusW(Bus_W), .BusR(R12));
  FRU fru_28 (.CLK(CLK), .RegWrite(Reg_Write), .RegEn(S16), .BusW(Bus_W), .BusR(R16));
  FRU fru_29 (.CLK(CLK), .RegWrite(Reg_Write), .RegEn(S20), .BusW(Bus_W), .BusR(R20));
  FRU fru_30 (.CLK(CLK), .RegWrite(Reg_Write), .RegEn(S24), .BusW(Bus_W), .BusR(R24));
  FRU fru_31 (.CLK(CLK), .RegWrite(Reg_Write), .RegEn(S28), .BusW(Bus_W), .BusR(R28));
  RegisterSelector registerselector_2 (
    .Register_S(RB), .R1(R1), .R2(R2), .R3(R3), .R4(R4), .R5(R5), .R6(R6), .R7(R7), .R8(R8), .R9(R9),
    .R10(R10), .R11(R11), .R12(R12), .R13(R13), .R14(R14), .R15(R15), .R16(R16), .R17(R17), .R18(R18),
    .R19(R19), .R20(R20), .R21(R21), .R22(R22), .R23(R23), .R24(R24), .R25(R25), .R26(R26), .R27(R27),
    .R28(R28), .R29(R29), .R30(R30), .R31(R31), .out_33(Bus_B));
endmodule
