// Logisim project RegisterFileTestBench.circ as structural Verilog: 1 circuit, main circuit main
module main (
  input  [2:0] in_1,
  input  [2:0] in_2,
  input  [2:0] in_3,
  input  [15:0] in_4,
  output [15:0] out_5,
  output [15:0] out_6,
  output [15:0] out_7,
  output [15:0] out_8,
  output [15:0] out_9,
  output [15:0] out_10,
  output [15:0] out_11,
  output [15:0] out_12,
  output [15:0] out_13
);

  wire button_1_out, clock_1_out;

  Clock clock_1 (.out(clock_1_out));
  Button button_1 (.out(button_1_out));
  RegisterFile registerfile_1 (
    .Reg_Write(button_1_out), .CLK(clock_1_out), .RA(in_1), .RB(in_2), .RW(in_3), .Bus_W(in_4),
    .Bus_A(out_5), .Bus_B(out_6), .R1(out_7), .R2(out_8), .R3(out_9), .R4(out_10), .R5(out_11), .R6(out_12),
    .R7(out_13));

  // Other names for the same wires on the sheet: R1[15:0] = out_7; R2[15:0] = out_8; R3[15:0] = out_9;
  //   R4[15:0] = out_10; R5[15:0] = out_11; R6[15:0] = out_12; R7[15:0] = out_13
endmodule
