// Logisim project RegisterSelectorSC.circ as structural Verilog: 1 circuit, main circuit RegisterSelector
module RegisterSelector (
  input  [4:0] Register_S,
  input  [31:0] R1,
  input  [31:0] R2,
  input  [31:0] R3,
  input  [31:0] R4,
  input  [31:0] R5,
  input  [31:0] R6,
  input  [31:0] R7,
  input  [31:0] R8,
  input  [31:0] R9,
  input  [31:0] R10,
  input  [31:0] R11,
  input  [31:0] R12,
  input  [31:0] R13,
  input  [31:0] R14,
  input  [31:0] R15,
  input  [31:0] R16,
  input  [31:0] R17,
  input  [31:0] R18,
  input  [31:0] R19,
  input  [31:0] R20,
  input  [31:0] R21,
  input  [31:0] R22,
  input  [31:0] R23,
  input  [31:0] R24,
  input  [31:0] R25,
  input  [31:0] R26,
  input  [31:0] R27,
  input  [31:0] R28,
  input  [31:0] R29,
  input  [31:0] R30,
  input  [31:0] R31,
  output [31:0] out_33
);

  wire S0, S1, S2, S3, S4, S5, S6, S7, S8, S9, S10, S11, S12, S13, S14, S15, S16, S17, S18, S19, S20, S21,
       S22, S23, S24, S25, S26, S27, S28, S29, S30, S31;
  wire [31:0] bit_extender_1_out;

  assign bit_extender_1_out = {{31{1'b0}}, 1'b0};  // Bit_Extender bit_extender_1
  assign out_33 = S0 ? bit_extender_1_out : 32'bz;  // Controlled_Buffer controlled_buffer_1
  assign out_33 = S1 ? R1 : 32'bz;  // Controlled_Buffer controlled_buffer_2
  assign out_33 = S2 ? R2 : 32'bz;  // Controlled_Buffer controlled_buffer_3
  assign out_33 = S3 ? R3 : 32'bz;  // Controlled_Buffer controlled_buffer_4
  assign out_33 = S4 ? R4 : 32'bz;  // Controlled_Buffer controlled_buffer_5
  assign out_33 = S5 ? R5 : 32'bz;  // Controlled_Buffer controlled_buffer_6
  assign out_33 = S6 ? R6 : 32'bz;  // Controlled_Buffer controlled_buffer_7
  assign out_33 = S7 ? R7 : 32'bz;  // Controlled_Buffer controlled_buffer_8
  assign out_33 = S8 ? R8 : 32'bz;  // Controlled_Buffer controlled_buffer_9
  assign out_33 = S9 ? R9 : 32'bz;  // Controlled_Buffer controlled_buffer_10
  assign out_33 = S10 ? R10 : 32'bz;  // Controlled_Buffer controlled_buffer_11
  assign out_33 = S11 ? R11 : 32'bz;  // Controlled_Buffer controlled_buffer_12
  assign out_33 = S12 ? R12 : 32'bz;  // Controlled_Buffer controlled_buffer_13
  assign out_33 = S13 ? R13 : 32'bz;  // Controlled_Buffer controlled_buffer_14
  assign out_33 = S14 ? R14 : 32'bz;  // Controlled_Buffer controlled_buffer_15
  assign out_33 = S15 ? R15 : 32'bz;  // Controlled_Buffer controlled_buffer_16
  assign out_33 = S16 ? R16 : 32'bz;  // Controlled_Buffer controlled_buffer_17
  assign out_33 = S17 ? R17 : 32'bz;  // Controlled_Buffer controlled_buffer_18
  assign out_33 = S18 ? R18 : 32'bz;  // Controlled_Buffer controlled_buffer_19
  assign out_33 = S19 ? R19 : 32'bz;  // Controlled_Buffer controlled_buffer_20
  assign out_33 = S20 ? R20 : 32'bz;  // Controlled_Buffer controlled_buffer_21
  assign out_33 = S21 ? R21 : 32'bz;  // Controlled_Buffer controlled_buffer_22
  assign out_33 = S22 ? R22 : 32'bz;  // Controlled_Buffer controlled_buffer_23
  assign out_33 = S23 ? R23 : 32'bz;  // Controlled_Buffer controlled_buffer_24
  assign out_33 = S24 ? R24 : 32'bz;  // Controlled_Buffer controlled_buffer_25
  assign out_33 = S25 ? R25 : 32'bz;  // Controlled_Buffer controlled_buffer_26
  assign out_33 = S26 ? R26 : 32'bz;  // Controlled_Buffer controlled_buffer_27
  assign out_33 = S27 ? R27 : 32'bz;  // Controlled_Buffer controlled_buffer_28
  assign out_33 = S28 ? R28 : 32'bz;  // Controlled_Buffer controlled_buffer_29
  assign out_33 = S29 ? R29 : 32'bz;  // Controlled_Buffer controlled_buffer_30
  assign out_33 = S30 ? R30 : 32'bz;  // Controlled_Buffer controlled_buffer_31
  assign out_33 = S31 ? R31 : 32'bz;  // Controlled_Buffer controlled_buffer_32
  Decoder #(.enable("false"), .select(5)) decoder_1 (
    .out0(S0), .out1(S1), .out2(S2), .out3(S3), .out4(S4), .out5(S5), .out6(S6), .out7(S7), .out8(S8),
    .out9(S9), .out10(S10), .out11(S11), .out12(S12), .out13(S13), .out14(S14), .out15(S15), .out16(S16),
    .out17(S17), .out18(S18), .out19(S19), .out20(S20), .out21(S21), .out22(S22), .out23(S23), .out24(S24),
    .out25(S25), .out26(S26), .out27(S27), .out28(S28), .out29(S29), .out30(S30), .out31(S31),
    .sel(Register_S));

  // Other names for the same wires on the sheet: Register_R[31:0] = out_33
endmodule
