// Logisim project RotateRight.circ as structural Verilog: 1 circuit, main circuit RotateRight
module RotateRight (
  input  [15:0] Operand,
  input  [3:0] SA,
  output [15:0] Operand_2
);

  Shifter #(.width(16), .shift("rr")) shifter_1 (.in(Operand), .\dist (SA), .out(Operand_2));

  // Other names for the same wires on the sheet: Output[15:0] = Operand_2
endmodule
