// Logisim project ShiftLeftLogically.circ as structural Verilog: 1 circuit, main circuit SLL
module SLL (
  input  [15:0] Operand,
  input  [3:0] Shift_Amount,
  output [15:0] Output
);

  Multiplexer #(.select(4), .enable("false")) multiplexer_1 (
    .in0(Operand[0]), .in1(1'b0), .in2(1'b0), .in3(1'b0), .in4(1'b0), .in5(1'b0), .in6(1'b0), .in7(1'b0),
    .in8(1'b0), .in9(1'b0), .in10(1'b0), .in11(1'b0), .in12(1'b0), .in13(1'b0), .in14(1'b0), .in15(1'b0),
    .out(Output[0]), .sel(Shift_Amount));
  Multiplexer #(.select(4), .enable("false")) multiplexer_2 (
    .in0(Operand[1]), .in1(Operand[0]), .in2(1'b0), .in3(1'b0), .in4(1'b0), .in5(1'b0), .in6(1'b0),
    .in7(1'b0), .in8(1'b0), .in9(1'b0), .in10(1'b0), .in11(1'b0), .in12(1'b0), .in13(1'b0), .in14(1'b0),
    .in15(1'b0), .out(Output[1]), .sel(Shift_Amount));
  Multiplexer #(.select(4), .enable("false")) multiplexer_3 (
    .in0(Operand[2]), .in1(Operand[1]), .in2(Operand[0]), .in3(1'b0), .in4(1'b0), .in5(1'b0), .in6(1'b0),
    .in7(1'b0), .in8(1'b0), .in9(1'b0), .in10(1'b0), .in11(1'b0), .in12(1'b0), .in13(1'b0), .in14(1'b0),
    .in15(1'b0), .out(Output[2]), .sel(Shift_Amount));
  Multiplexer #(.select(4), .enable("false")) multiplexer_4 (
    .in0(Operand[3]), .in1(Operand[2]), .in2(Operand[1]), .in3(Operand[0]), .in4(1'b0), .in5(1'b0),
    .in6(1'b0), .in7(1'b0), .in8(1'b0), .in9(1'b0), .in10(1'b0), .in11(1'b0), .in12(1'b0), .in13(1'b0),
    .in14(1'b0), .in15(1'b0), .out(Output[3]), .sel(Shift_Amount));
  Multiplexer #(.select(4), .enable("false")) multiplexer_5 (
    .in0(Operand[4]), .in1(Operand[3]), .in2(Operand[2]), .in3(Operand[1]), .in4(Operand[0]), .in5(1'b0),
    .in6(1'b0), .in7(1'b0), .in8(1'b0), .in9(1'b0), .in10(1'b0), .in11(1'b0), .in12(1'b0), .in13(1'b0),
    .in14(1'b0), .in15(1'b0), .out(Output[4]), .sel(Shift_Amount));
  Multiplexer #(.select(4), .enable("false")) multiplexer_6 (
    .in0(Operand[5]), .in1(Operand[4]), .in2(Operand[3]), .in3(Operand[2]), .in4(Operand[1]),
    .in5(Operand[0]), .in6(1'b0), .in7(1'b0), .in8(1'b0), .in9(1'b0), .in10(1'b0), .in11(1'b0), .in12(1'b0),
    .in13(1'b0), .in14(1'b0), .in15(1'b0), .out(Output[5]), .sel(Shift_Amount));
  Multiplexer #(.select(4), .enable("false")) multiplexer_7 (
    .in0(Operand[6]), .in1(Operand[5]), .in2(Operand[4]), .in3(Operand[3]), .in4(Operand[2]),
    .in5(Operand[1]), .in6(Operand[0]), .in7(1'b0), .in8(1'b0), .in9(1'b0), .in10(1'b0), .in11(1'b0),
    .in12(1'b0), .in13(1'b0), .in14(1'b0), .in15(1'b0), .out(Output[6]), .sel(Shift_Amount));
  Multiplexer #(.select(4), .enable("false")) multiplexer_8 (
    .in0(Operand[7]), .in1(Operand[6]), .in2(Operand[5]), .in3(Operand[4]), .in4(Operand[3]),
    .in5(Operand[2]), .in6(Operand[1]), .in7(Operand[0]), .in8(1'b0), .in9(1'b0), .in10(1'b0), .in11(1'b0),
    .in12(1'b0), .in13(1'b0), .in14(1'b0), .in15(1'b0), .out(Output[7]), .sel(Shift_Amount));
  Multiplexer #(.select(4), .enable("false")) multiplexer_9 (
    .in0(Operand[8]), .in1(Operand[7]), .in2(Operand[6]), .in3(Operand[5]), .in4(Operand[4]),
    .in5(Operand[3]), .in6(Operand[2]), .in7(Operand[1]), .in8(Operand[0]), .in9(1'b0), .in10(1'b0),
    .in11(1'b0), .in12(1'b0), .in13(1'b0), .in14(1'b0), .in15(1'b0), .out(Output[8]), .sel(Shift_Amount));
  Multiplexer #(.select(4), .enable("false")) multiplexer_10 (
    .in0(Operand[9]), .in1(Operand[8]), .in2(Operand[7]), .in3(Operand[6]), .in4(Operand[5]),
    .in5(Operand[4]), .in6(Operand[3]), .in7(Operand[2]), .in8(Operand[1]), .in9(Operand[0]), .in10(1'b0),
    .in11(1'b0), .in12(1'b0), .in13(1'b0), .in14(1'b0), .in15(1'b0), .out(Output[9]), .sel(Shift_Amount));
  Multiplexer #(.select(4), .enable("false")) multiplexer_11 (
    .in0(Operand[10]), .in1(Operand[9]), .in2(Operand[8]), .in3(Operand[7]), .in4(Operand[6]),
    .in5(Operand[5]), .in6(Operand[4]), .in7(Operand[3]), .in8(Operand[2]), .in9(Operand[1]),
    .in10(Operand[0]), .in11(1'b0), .in12(1'b0), .in13(1'b0), .in14(1'b0), .in15(1'b0), .out(Output[10]),
    .sel(Shift_Amount));
  Multiplexer #(.select(4), .enable("false")) multiplexer_12 (
    .in0(Operand[11]), .in1(Operand[10]), .in2(Operand[9]), .in3(Operand[8]), .in4(Operand[7]),
    .in5(Operand[6]), .in6(Operand[5]), .in7(Operand[4]), .in8(Operand[3]), .in9(Operand[2]),
    .in10(Operand[1]), .in11(Operand[0]), .in12(1'b0), .in13(1'b0), .in14(1'b0), .in15(1'b0),
    .out(Output[11]), .sel(Shift_Amount));
  Multiplexer #(.select(4), .enable("false")) multiplexer_13 (
    .in0(Operand[12]), .in1(Operand[11]), .in2(Operand[10]), .in3(Operand[9]), .in4(Operand[8]),
    .in5(Operand[7]), .in6(Operand[6]), .in7(Operand[5]), .in8(Operand[4]), .in9(Operand[3]),
    .in10(Operand[2]), .in11(Operand[1]), .in12(Operand[0]), .in13(1'b0), .in14(1'b0), .in15(1'b0),
    .out(Output[12]), .sel(Shift_Amount));
  Multiplexer #(.select(4), .enable("false")) multiplexer_14 (
    .in0(Operand[13]), .in1(Operand[12]), .in2(Operand[11]), .in3(Operand[10]), .in4(Operand[9]),
    .in5(Operand[8]), .in6(Operand[7]), .in7(Operand[6]), .in8(Operand[5]), .in9(Operand[4]),
    .in10(Operand[3]), .in11(Operand[2]), .in12(Operand[1]), .in13(Operand[0]), .in14(1'b0), .in15(1'b0),
    .out(Output[13]), .sel(Shift_Amount));
  Multiplexer #(.select(4), .enable("false")) multiplexer_15 (
    .in0(Operand[14]), .in1(Operand[13]), .in2(Operand[12]), .in3(Operand[11]), .in4(Operand[10]),
    .in5(Operand[9]), .in6(Operand[8]), .in7(Operand[7]), .in8(Operand[6]), .in9(Operand[5]),
    .in10(Operand[4]), .in11(Operand[3]), .in12(Operand[2]), .in13(Operand[1]), .in14(Operand[0]),
    .in15(1'b0), .out(Output[14]), .sel(Shift_Amount));
  Multiplexer #(.select(4), .enable("false")) multiplexer_16 (
    .in0(Operand[15]), .in1(Operand[14]), .in2(Operand[13]), .in3(Operand[12]), .in4(Operand[11]),
    .in5(Operand[10]), .in6(Operand[9]), .in7(Operand[8]), .in8(Operand[7]), .in9(Operand[6]),
    .in10(Operand[5]), .in11(Operand[4]), .in12(Operand[3]), .in13(Operand[2]), .in14(Operand[1]),
    .in15(Operand[0]), .out(Output[15]), .sel(Shift_Amount));

  // Other names for the same wires on the sheet: B0 = Operand[0]; B1 = Operand[1]; B2 = Operand[2]; B3 = Operand[3];
  //   B4 = Operand[4]; B5 = Operand[5]; B6 = Operand[6]; B7 = Operand[7]; B8 = Operand[8]; B9 = Operand[9];
  //   B10 = Operand[10]; B11 = Operand[11]; B12 = Operand[12]; B13 = Operand[13]; B14 = Operand[14];
  //   B15 = Operand[15]; S0 = Output[0]; S1 = Output[1]; S2 = Output[2]; S3 = Output[3]; S4 = Output[4];
  //   S5 = Output[5]; S6 = Output[6]; S7 = Output[7]; S8 = Output[8]; S9 = Output[9]; S10 = Output[10];
  //   S11 = Output[11]; S12 = Output[12]; S13 = Output[13]; S14 = Output[14]; S15 = Output[15];
  //   SA[3:0] = Shift_Amount
endmodule
