// Logisim project ShiftRightLogicallyArithmetically.circ as structural Verilog: 1 circuit, main circuit SRLA
module SRLA (
  input  [15:0] Operand,
  input  [3:0] Shift_Amount,
  input  Arithmetic_Shift,
  output [15:0] Output
);

  wire controlled_buffer_1_out, controlled_buffer_2_out, controlled_buffer_5_out, controlled_buffer_6_out,
       controlled_buffer_9_out, controlled_buffer_11_out, controlled_buffer_13_out, controlled_buffer_15_out,
       controlled_buffer_17_out, controlled_buffer_19_out, controlled_buffer_21_out,
       controlled_buffer_23_out, controlled_buffer_25_out, controlled_buffer_27_out,
       controlled_buffer_29_out, not_1_out, not_2_out, not_3_out, not_4_out, not_5_out, not_6_out, not_7_out,
       not_8_out, not_9_out, not_10_out, not_11_out, not_12_out, not_13_out, not_14_out, not_15_out;

  assign controlled_buffer_1_out = Arithmetic_Shift ? Operand[15] : 1'bz;  // Controlled_Buffer controlled_buffer_1
  assign controlled_buffer_2_out = Arithmetic_Shift ? Operand[15] : 1'bz;  // Controlled_Buffer controlled_buffer_2
  assign controlled_buffer_1_out = not_1_out ? 1'b0 : 1'bz;  // Controlled_Buffer controlled_buffer_3
  not not_1 (not_1_out, Arithmetic_Shift);
  assign controlled_buffer_2_out = not_2_out ? 1'b0 : 1'bz;  // Controlled_Buffer controlled_buffer_4
  not not_2 (not_2_out, Arithmetic_Shift);
  Multiplexer #(.select(4), .enable("false")) multiplexer_1 (
    .in0(Operand[15]), .in1(controlled_buffer_1_out), .in2(controlled_buffer_1_out),
    .in3(controlled_buffer_1_out), .in4(controlled_buffer_1_out), .in5(controlled_buffer_1_out),
    .in6(controlled_buffer_1_out), .in7(controlled_buffer_1_out), .in8(controlled_buffer_1_out),
    .in9(controlled_buffer_1_out), .in10(controlled_buffer_1_out), .in11(controlled_buffer_1_out),
    .in12(controlled_buffer_1_out), .in13(controlled_buffer_1_out), .in14(controlled_buffer_1_out),
    .in15(controlled_buffer_1_out), .out(Output[15]), .sel(Shift_Amount));
  Multiplexer #(.select(4), .enable("false")) multiplexer_2 (
    .in0(Operand[14]), .in1(Operand[15]), .in2(controlled_buffer_2_out), .in3(controlled_buffer_2_out),
    .in4(controlled_buffer_2_out), .in5(controlled_buffer_2_out), .in6(controlled_buffer_2_out),
    .in7(controlled_buffer_2_out), .in8(controlled_buffer_2_out), .in9(controlled_buffer_2_out),
    .in10(controlled_buffer_2_out), .in11(controlled_buffer_2_out), .in12(controlled_buffer_2_out),
    .in13(controlled_buffer_2_out), .in14(controlled_buffer_2_out), .in15(controlled_buffer_2_out),
    .out(Output[14]), .sel(Shift_Amount));
  assign controlled_buffer_5_out = Arithmetic_Shift ? Operand[15] : 1'bz;  // Controlled_Buffer controlled_buffer_5
  assign controlled_buffer_6_out = Arithmetic_Shift ? Operand[15] : 1'bz;  // Controlled_Buffer controlled_buffer_6
  Multiplexer #(.select(4), .enable("false")) multiplexer_3 (
    .in0(Operand[13]), .in1(Operand[14]), .in2(Operand[15]), .in3(controlled_buffer_5_out),
    .in4(controlled_buffer_5_out), .in5(controlled_buffer_5_out), .in6(controlled_buffer_5_out),
    .in7(controlled_buffer_5_out), .in8(controlled_buffer_5_out), .in9(controlled_buffer_5_out),
    .in10(controlled_buffer_5_out), .in11(controlled_buffer_5_out), .in12(controlled_buffer_5_out),
    .in13(controlled_buffer_5_out), .in14(controlled_buffer_5_out), .in15(controlled_buffer_5_out),
    .out(Output[13]), .sel(Shift_Amount));
  assign controlled_buffer_5_out = not_3_out ? 1'b0 : 1'bz;  // Controlled_Buffer controlled_buffer_7
  not not_3 (not_3_out, Arithmetic_Shift);
  assign controlled_buffer_6_out = not_4_out ? 1'b0 : 1'bz;  // Controlled_Buffer controlled_buffer_8
  not not_4 (not_4_out, Arithmetic_Shift);
  Multiplexer #(.select(4), .enable("false")) multiplexer_4 (
    .in0(Operand[12]), .in1(Operand[13]), .in2(Operand[14]), .in3(Operand[15]),
    .in4(controlled_buffer_6_out), .in5(controlled_buffer_6_out), .in6(controlled_buffer_6_out),
    .in7(controlled_buffer_6_out), .in8(controlled_buffer_6_out), .in9(controlled_buffer_6_out),
    .in10(controlled_buffer_6_out), .in11(controlled_buffer_6_out), .in12(controlled_buffer_6_out),
    .in13(controlled_buffer_6_out), .in14(controlled_buffer_6_out), .in15(controlled_buffer_6_out),
    .out(Output[12]), .sel(Shift_Amount));
  assign controlled_buffer_9_out = Arithmetic_Shift ? Operand[15] : 1'bz;  // Controlled_Buffer controlled_buffer_9
  Multiplexer #(.select(4), .enable("false")) multiplexer_5 (
    .in0(Operand[11]), .in1(Operand[12]), .in2(Operand[13]), .in3(Operand[14]), .in4(Operand[15]),
    .in5(controlled_buffer_9_out), .in6(controlled_buffer_9_out), .in7(controlled_buffer_9_out),
    .in8(controlled_buffer_9_out), .in9(controlled_buffer_9_out), .in10(controlled_buffer_9_out),
    .in11(controlled_buffer_9_out), .in12(controlled_buffer_9_out), .in13(controlled_buffer_9_out),
    .in14(controlled_buffer_9_out), .in15(controlled_buffer_9_out), .out(Output[11]), .sel(Shift_Amount));
  assign controlled_buffer_9_out = not_5_out ? 1'b0 : 1'bz;  // Controlled_Buffer controlled_buffer_10
  not not_5 (not_5_out, Arithmetic_Shift);
  assign controlled_buffer_11_out = Arithmetic_Shift ? Operand[15] : 1'bz;  // Controlled_Buffer controlled_buffer_11
  assign controlled_buffer_11_out = not_6_out ? 1'b0 : 1'bz;  // Controlled_Buffer controlled_buffer_12
  not not_6 (not_6_out, Arithmetic_Shift);
  Multiplexer #(.select(4), .enable("false")) multiplexer_6 (
    .in0(Operand[10]), .in1(Operand[11]), .in2(Operand[12]), .in3(Operand[13]), .in4(Operand[14]),
    .in5(Operand[15]), .in6(controlled_buffer_11_out), .in7(controlled_buffer_11_out),
    .in8(controlled_buffer_11_out), .in9(controlled_buffer_11_out), .in10(controlled_buffer_11_out),
    .in11(controlled_buffer_11_out), .in12(controlled_buffer_11_out), .in13(controlled_buffer_11_out),
    .in14(controlled_buffer_11_out), .in15(controlled_buffer_11_out), .out(Output[10]), .sel(Shift_Amount));
  assign controlled_buffer_13_out = Arithmetic_Shift ? Operand[15] : 1'bz;  // Controlled_Buffer controlled_buffer_13
  assign controlled_buffer_13_out = not_7_out ? 1'b0 : 1'bz;  // Controlled_Buffer controlled_buffer_14
  not not_7 (not_7_out, Arithmetic_Shift);
  assign controlled_buffer_15_out = not_8_out ? 1'b0 : 1'bz;  // Controlled_Buffer controlled_buffer_15
  assign controlled_buffer_15_out = Arithmetic_Shift ? Operand[15] : 1'bz;  // Controlled_Buffer controlled_buffer_16
  Multiplexer #(.select(4), .enable("false")) multiplexer_7 (
    .in0(Operand[9]), .in1(Operand[10]), .in2(Operand[11]), .in3(Operand[12]), .in4(Operand[13]),
    .in5(Operand[14]), .in6(Operand[15]), .in7(controlled_buffer_13_out), .in8(controlled_buffer_13_out),
    .in9(controlled_buffer_13_out), .in10(controlled_buffer_13_out), .in11(controlled_buffer_13_out),
    .in12(controlled_buffer_13_out), .in13(controlled_buffer_13_out), .in14(controlled_buffer_13_out),
    .in15(controlled_buffer_13_out), .out(Output[9]), .sel(Shift_Amount));
  Multiplexer #(.select(4), .enable("false")) multiplexer_8 (
    .in0(Operand[8]), .in1(Operand[9]), .in2(Operand[10]), .in3(Operand[11]), .in4(Operand[12]),
    .in5(Operand[13]), .in6(Operand[14]), .in7(Operand[15]), .in8(controlled_buffer_15_out),
    .in9(controlled_buffer_15_out), .in10(controlled_buffer_15_out), .in11(controlled_buffer_15_out),
    .in12(controlled_buffer_15_out), .in13(controlled_buffer_15_out), .in14(controlled_buffer_15_out),
    .in15(controlled_buffer_15_out), .out(Output[8]), .sel(Shift_Amount));
  not not_8 (not_8_out, Arithmetic_Shift);
  assign controlled_buffer_17_out = Arithmetic_Shift ? Operand[15] : 1'bz;  // Controlled_Buffer controlled_buffer_17
  assign controlled_buffer_17_out = not_9_out ? 1'b0 : 1'bz;  // Controlled_Buffer controlled_buffer_18
  not not_9 (not_9_out, Arithmetic_Shift);
  assign controlled_buffer_19_out = Arithmetic_Shift ? Operand[15] : 1'bz;  // Controlled_Buffer controlled_buffer_19
  assign controlled_buffer_19_out = not_10_out ? 1'b0 : 1'bz;  // Controlled_Buffer controlled_buffer_20
  not not_10 (not_10_out, Arithmetic_Shift);
  Multiplexer #(.select(4), .enable("false")) multiplexer_9 (
    .in0(Operand[7]), .in1(Operand[8]), .in2(Operand[9]), .in3(Operand[10]), .in4(Operand[11]),
    .in5(Operand[12]), .in6(Operand[13]), .in7(Operand[14]), .in8(Operand[15]),
    .in9(controlled_buffer_17_out), .in10(controlled_buffer_17_out), .in11(controlled_buffer_17_out),
    .in12(controlled_buffer_17_out), .in13(controlled_buffer_17_out), .in14(controlled_buffer_17_out),
    .in15(controlled_buffer_17_out), .out(Output[7]), .sel(Shift_Amount));
  Multiplexer #(.select(4), .enable("false")) multiplexer_10 (
    .in0(Operand[6]), .in1(Operand[7]), .in2(Operand[8]), .in3(Operand[9]), .in4(Operand[10]),
    .in5(Operand[11]), .in6(Operand[12]), .in7(Operand[13]), .in8(Operand[14]), .in9(Operand[15]),
    .in10(controlled_buffer_19_out), .in11(controlled_buffer_19_out), .in12(controlled_buffer_19_out),
    .in13(controlled_buffer_19_out), .in14(controlled_buffer_19_out), .in15(controlled_buffer_19_out),
    .out(Output[6]), .sel(Shift_Amount));
  assign controlled_buffer_21_out = not_11_out ? 1'b0 : 1'bz;  // Controlled_Buffer controlled_buffer_21
  assign controlled_buffer_21_out = Arithmetic_Shift ? Operand[15] : 1'bz;  // Controlled_Buffer controlled_buffer_22
  not not_11 (not_11_out, Arithmetic_Shift);
  assign controlled_buffer_23_out = not_12_out ? 1'b0 : 1'bz;  // Controlled_Buffer controlled_buffer_23
  assign controlled_buffer_23_out = Arithmetic_Shift ? Operand[15] : 1'bz;  // Controlled_Buffer controlled_buffer_24
  Multiplexer #(.select(4), .enable("false")) multiplexer_11 (
    .in0(Operand[5]), .in1(Operand[6]), .in2(Operand[7]), .in3(Operand[8]), .in4(Operand[9]),
    .in5(Operand[10]), .in6(Operand[11]), .in7(Operand[12]), .in8(Operand[13]), .in9(Operand[14]),
    .in10(Operand[15]), .in11(controlled_buffer_21_out), .in12(controlled_buffer_21_out),
    .in13(controlled_buffer_21_out), .in14(controlled_buffer_21_out), .in15(controlled_buffer_21_out),
    .out(Output[5]), .sel(Shift_Amount));
  Multiplexer #(.select(4), .enable("false")) multiplexer_12 (
    .in0(Operand[4]), .in1(Operand[5]), .in2(Operand[6]), .in3(Operand[7]), .in4(Operand[8]),
    .in5(Operand[9]), .in6(Operand[10]), .in7(Operand[11]), .in8(Operand[12]), .in9(Operand[13]),
    .in10(Operand[14]), .in11(Operand[15]), .in12(controlled_buffer_23_out), .in13(controlled_buffer_23_out),
    .in14(controlled_buffer_23_out), .in15(controlled_buffer_23_out), .out(Output[4]), .sel(Shift_Amount));
  not not_12 (not_12_out, Arithmetic_Shift);
  assign controlled_buffer_25_out = Arithmetic_Shift ? Operand[15] : 1'bz;  // Controlled_Buffer controlled_buffer_25
  assign controlled_buffer_25_out = not_13_out ? 1'b0 : 1'bz;  // Controlled_Buffer controlled_buffer_26
  not not_13 (not_13_out, Arithmetic_Shift);
  assign controlled_buffer_27_out = Arithmetic_Shift ? Operand[15] : 1'bz;  // Controlled_Buffer controlled_buffer_27
  assign controlled_buffer_27_out = not_14_out ? 1'b0 : 1'bz;  // Controlled_Buffer controlled_buffer_28
  not not_14 (not_14_out, Arithmetic_Shift);
  Multiplexer #(.select(4), .enable("false")) multiplexer_13 (
    .in0(Operand[3]), .in1(Operand[4]), .in2(Operand[5]), .in3(Operand[6]), .in4(Operand[7]),
    .in5(Operand[8]), .in6(Operand[9]), .in7(Operand[10]), .in8(Operand[11]), .in9(Operand[12]),
    .in10(Operand[13]), .in11(Operand[14]), .in12(Operand[15]), .in13(controlled_buffer_25_out),
    .in14(controlled_buffer_25_out), .in15(controlled_buffer_25_out), .out(Output[3]), .sel(Shift_Amount));
  Multiplexer #(.select(4), .enable("false")) multiplexer_14 (
    .in0(Operand[2]), .in1(Operand[3]), .in2(Operand[4]), .in3(Operand[5]), .in4(Operand[6]),
    .in5(Operand[7]), .in6(Operand[8]), .in7(Operand[9]), .in8(Operand[10]), .in9(Operand[11]),
    .in10(Operand[12]), .in11(Operand[13]), .in12(Operand[14]), .in13(Operand[15]),
    .in14(controlled_buffer_27_out), .in15(controlled_buffer_27_out), .out(Output[2]), .sel(Shift_Amount));
  assign controlled_buffer_29_out = not_15_out ? 1'b0 : 1'bz;  // Controlled_Buffer controlled_buffer_29
  assign controlled_buffer_29_out = Arithmetic_Shift ? Operand[15] : 1'bz;  // Controlled_Buffer controlled_buffer_30
  not not_15 (not_15_out, Arithmetic_Shift);
  Multiplexer #(.select(4), .enable("false")) multiplexer_15 (
    .in0(Operand[1]), .in1(Operand[2]), .in2(Operand[3]), .in3(Operand[4]), .in4(Operand[5]),
    .in5(Operand[6]), .in6(Operand[7]), .in7(Operand[8]), .in8(Operand[9]), .in9(Operand[10]),
    .in10(Operand[11]), .in11(Operand[12]), .in12(Operand[13]), .in13(Operand[14]), .in14(Operand[15]),
    .in15(controlled_buffer_29_out), .out(Output[1]), .sel(Shift_Amount));
  Multiplexer #(.select(4), .enable("false")) multiplexer_16 (
    .in0(Operand[0]), .in1(Operand[1]), .in2(Operand[2]), .in3(Operand[3]), .in4(Operand[4]),
    .in5(Operand[5]), .in6(Operand[6]), .in7(Operand[7]), .in8(Operand[8]), .in9(Operand[9]),
    .in10(Operand[10]), .in11(Operand[11]), .in12(Operand[12]), .in13(Operand[13]), .in14(Operand[14]),
    .in15(Operand[15]), .out(Output[0]), .sel(Shift_Amount));

  // Other names for the same wires on the sheet: A = Arithmetic_Shift; B0 = Operand[0]; B1 = Operand[1];
  //   B2 = Operand[2]; B3 = Operand[3]; B4 = Operand[4]; B5 = Operand[5]; B6 = Operand[6]; B7 = Operand[7];
  //   B8 = Operand[8]; B9 = Operand[9]; B10 = Operand[10]; B11 = Operand[11]; B12 = Operand[12]; B13 = Operand[13];
  //   B14 = Operand[14]; B15 = Operand[15]; MSB = Operand[15]; S0 = Output[0]; S1 = Output[1]; S2 = Output[2];
  //   S3 = Output[3]; S4 = Output[4]; S5 = Output[5]; S6 = Output[6]; S7 = Output[7]; S8 = Output[8]; S9 = Output[9];
  //   S10 = Output[10]; S11 = Output[11]; S12 = Output[12]; S13 = Output[13]; S14 = Output[14]; S15 = Output[15];
  //   SA[3:0] = Shift_Amount
endmodule
