// Logisim project SingleCycle.circ as structural Verilog: 1 circuit, main circuit main
module main (
);

  wire ALUSrc, clk, JumpOP, MemoryRead, MemoryWrite, not_1_out, RegWrite, signExtend, ZeroFlag;
  wire [1:0] BranchOP, F, PCSrc, RegDest, RegisterWSrc;
  wire [2:0] multiplexer_2_out, Rd, Rs, Rt;
  wire [3:0] ALUop;
  wire [4:0] Imm5, Opcode;
  wire [10:0] Imm11;
  wire [15:0] ALUout, bit_extender_1_out, bit_extender_2_out, bit_extender_3_out, BranchPC,
       extendedImmediate, JumpPC, MemoryData, multiplexer_1_out, multiplexer_4_out, OperandA, OperandB, PC,
       PC_1, R1, R2, R3, R4, R5, R6, R7, RegisterWrite, rom_1_data, ShiftedImm;

  // Probe on PCSrc
  Clock clock_1 (.out(clk));
  Multiplexer #(.select(2), .width(16), .enable("false")) multiplexer_1 (
    .in0({16{1'b0}}), .in1(BranchPC), .in2(JumpPC), .in3(PC_1), .out(multiplexer_1_out), .sel(PCSrc));
  Register #(.width(16)) register_1 (.D(multiplexer_1_out), .Q(PC), .clk(clk));  // open: en, clr
  ControlUnit controlunit_1 (
    .Opcode(Opcode), .Function(F), .ALUop(ALUop), .ALUSrc(ALUSrc), .signExtend(signExtend),
    .RegWrite(RegWrite), .RegDest(RegDest), .RegWSrc(RegisterWSrc), .memoryRead(MemoryRead),
    .memoryWrite(MemoryWrite), .PCSrc(PCSrc), .BrachOP(BranchOP), .JumpOP(JumpOP));
  Adder #(.width(16)) adder_1 (.a(16'h1), .b(PC), .out(PC_1), .cin(1'b0));  // open: cout
  JumpControl jumpcontrol_1 (.PC(PC), .Rs(OperandA), .Imm1(Imm11), .newPC(JumpPC), .JOperation(JumpOP));
  ROM #(.addrWidth(16), .dataWidth(16)) rom_1 (.addr(PC), .data(rom_1_data), .sel(1'b1));
  // Probe on rom_1_data
  // Probe on Opcode
  InstructionSplitter instructionsplitter_1 (
    .Instruction(rom_1_data), .Op(Opcode), .F(F), .Rd(Rd), .Rs(Rs), .Rt(Rt), .Imm5(Imm5), .Imm11(Imm11));
  // Probe on BranchOP
  // Probe on Rs
  // Probe on Rt
  // Probe on Rd
  BranchControl branchcontrol_1 (
    .Operation(BranchOP), .Zero(ZeroFlag), .Less_Than(ALUout[0]), .Imm5(Imm5), .PC(PC_1), .newPC(BranchPC));
  // Probe on RegDest
  // Probe on R1
  // Probe on R2
  // Probe on R3
  // Probe on R4
  // Probe on R5
  // Probe on R6
  // Probe on R7
  Multiplexer #(.select(2), .width(3), .enable("false")) multiplexer_2 (
    .in0(Rt), .in1(Rd), .in2(3'b001), .in3(3'b111), .out(multiplexer_2_out), .sel(RegDest));
  Multiplexer #(.select(2), .width(16), .enable("false")) multiplexer_3 (
    .in0(ALUout), .in1(MemoryData), .in2(ShiftedImm), .in3(PC_1), .out(RegisterWrite), .sel(RegisterWSrc));
  RegisterFile registerfile_1 (
    .Reg_Write(RegWrite), .CLK(clk), .RA(Rs), .RB(Rt), .RW(multiplexer_2_out), .Bus_W(RegisterWrite),
    .Bus_A(OperandA), .Bus_B(OperandB), .R1(R1), .R2(R2), .R3(R3), .R4(R4), .R5(R5), .R6(R6), .R7(R7));
  Multiplexer #(.width(16), .enable("false")) multiplexer_4 (
    .in0(OperandB), .in1(extendedImmediate), .out(multiplexer_4_out), .sel(ALUSrc));
  assign bit_extender_1_out = {{11{1'b0}}, Imm5};  // Bit_Extender bit_extender_1
  assign bit_extender_2_out = {{11{Imm5[4]}}, Imm5};  // Bit_Extender bit_extender_2
  assign bit_extender_3_out = {{5{1'b0}}, Imm11};  // Bit_Extender bit_extender_3
  assign extendedImmediate = not_1_out ? bit_extender_1_out : 16'bz;  // Controlled_Buffer controlled_buffer_1
  not not_1 (not_1_out, signExtend);
  assign extendedImmediate = signExtend ? bit_extender_2_out : 16'bz;  // Controlled_Buffer controlled_buffer_2
  Shifter #(.width(16)) shifter_1 (.in(bit_extender_3_out), .\dist (4'b0101), .out(ShiftedImm));
  ALU alu_1 (.in_1(ALUop), .in_2(OperandA), .in_3(multiplexer_4_out), .out_5(ZeroFlag), .out_6(ALUout));  // open: out_4
  Data_Memory data_memory_1 (
    .CLK(clk), .Memory_Enable(1'b1), .Memory_Read(MemoryRead), .Memory_Write(MemoryWrite), .Address(ALUout),
    .Data_In(OperandB), .Data_Out(MemoryData));

  // Other names for the same wires on the sheet: SLT = ALUout[0]; RsValue[15:0] = OperandA; RtValue[15:0] = OperandB

  // Notes on the sheet:
  //   contents of rom_1 (hex, n*v repeats v):
  //   3941 3a82 3803 38c4 708c 3852 7894 f002 385b 8894 f002 3864 80a2 f002 3fd2 681a 601d f801 1038
endmodule
