// Logisim project file.circ as structural Verilog: 3 circuits, main circuit alu arithmetic
module alu_arithmetic (
  input  Set,
  input  SetUnsigned,
  input  Sub,
  input  [15:0] in_4,
  input  [15:0] in_5,
  output Zero,
  output Overflow,
  output [15:0] Output
);

  wire addersubtractor_1_carryout, addersubtractor_2_carryout, addersubtractor_3_carryout,
       addersubtractor_4_carryout, addersubtractor_5_carryout, addersubtractor_6_carryout,
       addersubtractor_7_carryout, addersubtractor_8_carryout, addersubtractor_9_carryout,
       addersubtractor_10_carryout, addersubtractor_11_carryout, addersubtractor_12_carryout,
       addersubtractor_13_carryout, addersubtractor_14_carryout, C14, C15, controlled_buffer_1_out,
       multiplexer_4_out, not_1_out, not_2_out, or_1_out, or_2_out, or_3_out, or_4_out, or_5_out, or_6_out,
       or_7_out, or_8_out, or_9_out, or_10_out, or_11_out, or_12_out, or_13_out, or_14_out, or_15_out,
       or_16_out, z0, z1, z2, z3, z4, z5, z6, z7, z8, z9, z10, z11, z12, z13, z14, z15;

  AdderSubtractor addersubtractor_1 (
    .A(in_5[0]), .B(in_4[0]), .CarryIn(Sub), .BNegate(Sub), .CarryOut(addersubtractor_1_carryout), .Out(z0));
  AdderSubtractor addersubtractor_2 (
    .A(in_5[1]), .B(in_4[1]), .CarryIn(addersubtractor_1_carryout), .BNegate(Sub),
    .CarryOut(addersubtractor_2_carryout), .Out(z1));
  AdderSubtractor addersubtractor_3 (
    .A(in_5[2]), .B(in_4[2]), .CarryIn(addersubtractor_2_carryout), .BNegate(Sub),
    .CarryOut(addersubtractor_3_carryout), .Out(z2));
  AdderSubtractor addersubtractor_4 (
    .A(in_5[3]), .B(in_4[3]), .CarryIn(addersubtractor_3_carryout), .BNegate(Sub),
    .CarryOut(addersubtractor_4_carryout), .Out(z3));
  AdderSubtractor addersubtractor_5 (
    .A(in_5[4]), .B(in_4[4]), .CarryIn(addersubtractor_4_carryout), .BNegate(Sub),
    .CarryOut(addersubtractor_5_carryout), .Out(z4));
  AdderSubtractor addersubtractor_6 (
    .A(in_5[5]), .B(in_4[5]), .CarryIn(addersubtractor_5_carryout), .BNegate(Sub),
    .CarryOut(addersubtractor_6_carryout), .Out(z5));
  AdderSubtractor addersubtractor_7 (
    .A(in_5[6]), .B(in_4[6]), .CarryIn(addersubtractor_6_carryout), .BNegate(Sub),
    .CarryOut(addersubtractor_7_carryout), .Out(z6));
  AdderSubtractor addersubtractor_8 (
    .A(in_5[7]), .B(in_4[7]), .CarryIn(addersubtractor_7_carryout), .BNegate(Sub),
    .CarryOut(addersubtractor_8_carryout), .Out(z7));
  AdderSubtractor addersubtractor_9 (
    .A(in_5[8]), .B(in_4[8]), .CarryIn(addersubtractor_8_carryout), .BNegate(Sub),
    .CarryOut(addersubtractor_9_carryout), .Out(z8));
  AdderSubtractor addersubtractor_10 (
    .A(in_5[9]), .B(in_4[9]), .CarryIn(addersubtractor_9_carryout), .BNegate(Sub),
    .CarryOut(addersubtractor_10_carryout), .Out(z9));
  AdderSubtractor addersubtractor_11 (
    .A(in_5[10]), .B(in_4[10]), .CarryIn(addersubtractor_10_carryout), .BNegate(Sub),
    .CarryOut(addersubtractor_11_carryout), .Out(z10));
  AdderSubtractor addersubtractor_12 (
    .A(in_5[11]), .B(in_4[11]), .CarryIn(addersubtractor_11_carryout), .BNegate(Sub),
    .CarryOut(addersubtractor_12_carryout), .Out(z11));
  AdderSubtractor addersubtractor_13 (
    .A(in_5[12]), .B(in_4[12]), .CarryIn(addersubtractor_12_carryout), .BNegate(Sub),
    .CarryOut(addersubtractor_13_carryout), .Out(z12));
  AdderSubtractor addersubtractor_14 (
    .A(in_5[13]), .B(in_4[13]), .CarryIn(addersubtractor_13_carryout), .BNegate(Sub),
    .CarryOut(addersubtractor_14_carryout), .Out(z13));
  AdderSubtractor addersubtractor_15 (
    .A(in_5[14]), .B(in_4[14]), .CarryIn(addersubtractor_14_carryout), .BNegate(Sub), .CarryOut(C14),
    .Out(z14));
  AdderSubtractor addersubtractor_16 (
    .A(in_5[15]), .B(in_4[15]), .CarryIn(C14), .BNegate(Sub), .CarryOut(C15), .Out(z15));
  assign controlled_buffer_1_out = SetUnsigned ? 1'b0 : 1'bz;  // Controlled_Buffer controlled_buffer_1
  not not_1 (not_1_out, z15);
  Multiplexer #(.enable("false")) multiplexer_1 (.in0(z1), .in1(1'b0), .out(Output[1]), .sel(or_1_out));
  or or_1 (or_1_out, SetUnsigned, Set);
  Multiplexer #(.enable("false")) multiplexer_2 (.in0(z3), .in1(1'b0), .out(Output[3]), .sel(or_2_out));
  or or_2 (or_2_out, SetUnsigned, Set);
  Multiplexer #(.enable("false")) multiplexer_3 (.in0(z5), .in1(1'b0), .out(Output[5]), .sel(or_3_out));
  or or_3 (or_3_out, SetUnsigned, Set);
  or or_4 (or_4_out, SetUnsigned, Set);
  or or_5 (or_5_out, SetUnsigned, Set);
  or or_6 (or_6_out, SetUnsigned, Set);
  xor xor_1 (Overflow, C14, C15);
  Multiplexer #(.enable("false")) multiplexer_4 (
    .in0(z15), .in1(not_1_out), .out(multiplexer_4_out), .sel(controlled_buffer_1_out));
  assign controlled_buffer_1_out = not_2_out ? Overflow : 1'bz;  // Controlled_Buffer controlled_buffer_2
  not not_2 (not_2_out, SetUnsigned);
  Multiplexer #(.enable("false")) multiplexer_5 (.in0(z7), .in1(1'b0), .out(Output[7]), .sel(or_4_out));
  Multiplexer #(.enable("false")) multiplexer_6 (.in0(z9), .in1(1'b0), .out(Output[9]), .sel(or_5_out));
  Multiplexer #(.enable("false")) multiplexer_7 (.in0(z11), .in1(1'b0), .out(Output[11]), .sel(or_6_out));
  Multiplexer #(.enable("false")) multiplexer_8 (.in0(z13), .in1(1'b0), .out(Output[13]), .sel(or_7_out));
  or or_7 (or_7_out, SetUnsigned, Set);
  or or_8 (or_8_out, SetUnsigned, Set);
  Multiplexer #(.enable("false")) multiplexer_9 (.in0(z2), .in1(1'b0), .out(Output[2]), .sel(or_9_out));
  or or_9 (or_9_out, SetUnsigned, Set);
  Multiplexer #(.enable("false")) multiplexer_10 (.in0(z4), .in1(1'b0), .out(Output[4]), .sel(or_10_out));
  or or_10 (or_10_out, SetUnsigned, Set);
  Multiplexer #(.enable("false")) multiplexer_11 (.in0(z6), .in1(1'b0), .out(Output[6]), .sel(or_11_out));
  or or_11 (or_11_out, SetUnsigned, Set);
  Multiplexer #(.enable("false")) multiplexer_12 (.in0(z8), .in1(1'b0), .out(Output[8]), .sel(or_12_out));
  or or_12 (or_12_out, SetUnsigned, Set);
  Multiplexer #(.enable("false")) multiplexer_13 (.in0(z10), .in1(1'b0), .out(Output[10]), .sel(or_13_out));
  or or_13 (or_13_out, SetUnsigned, Set);
  or or_14 (or_14_out, SetUnsigned, Set);
  or or_15 (or_15_out, SetUnsigned, Set);
  Multiplexer #(.enable("false")) multiplexer_14 (.in0(z15), .in1(1'b0), .out(Output[15]), .sel(or_16_out));
  or or_16 (or_16_out, SetUnsigned, Set);
  Multiplexer #(.enable("false")) multiplexer_15 (.in0(z0), .in1(multiplexer_4_out), .out(Output[0]), .sel(or_8_out));
  Multiplexer #(.enable("false")) multiplexer_16 (.in0(z12), .in1(1'b0), .out(Output[12]), .sel(or_14_out));
  Multiplexer #(.enable("false")) multiplexer_17 (.in0(z14), .in1(1'b0), .out(Output[14]), .sel(or_15_out));
  nor nor_1 (Zero, z0, z1, z2, z3, z4, z5, z6, z7, z8, z15, z14, z13, z12, z11, z10, z9);

  // Other names for the same wires on the sheet: b0 = in_4[0]; b1 = in_4[1]; b2 = in_4[2]; b3 = in_4[3]; b4 = in_4[4];
  //   b5 = in_4[5]; b6 = in_4[6]; b7 = in_4[7]; b8 = in_4[8]; b9 = in_4[9]; b10 = in_4[10]; b11 = in_4[11];
  //   b12 = in_4[12]; b13 = in_4[13]; b14 = in_4[14]; b15 = in_4[15]; a0 = in_5[0]; a1 = in_5[1]; a2 = in_5[2];
  //   a3 = in_5[3]; a4 = in_5[4]; a5 = in_5[5]; a6 = in_5[6]; a7 = in_5[7]; a8 = in_5[8]; a9 = in_5[9];
  //   a10 = in_5[10]; a11 = in_5[11]; a12 = in_5[12]; a13 = in_5[13]; a14 = in_5[14]; a15 = in_5[15]; o0 = Output[0];
  //   o1 = Output[1]; o2 = Output[2]; o3 = Output[3]; o4 = Output[4]; o5 = Output[5]; o6 = Output[6]; o7 = Output[7];
  //   o8 = Output[8]; o9 = Output[9]; o10 = Output[10]; o11 = Output[11]; o12 = Output[12]; o13 = Output[13];
  //   o14 = Output[14]; o15 = Output[15]

  // Notes on the sheet:
  //   B
  //   A
endmodule

module AdderSubtractor (
  input  A,
  input  B,
  input  CarryIn,
  input  BNegate,
  output CarryOut,
  output Out
);

  wire ActualB, Bin;

  not not_1 (Bin, B);
  Multiplexer #(.enable("false")) multiplexer_1 (.in0(B), .in1(Bin), .out(ActualB), .sel(BNegate));
  Adder #(.width(1)) adder_1 (.a(A), .b(ActualB), .out(Out), .cin(CarryIn), .cout(CarryOut));

  // Other names for the same wires on the sheet: cin = CarryIn; cout = CarryOut
endmodule

module testBench (
  input  in_1,
  input  in_2,
  input  in_3
);

  wire clock_1_out;
  wire [6:0] counter_1_q;
  wire [15:0] ram_1_data, rom_1_data, rom_2_data;

  Counter #(.width(7), .max('h64)) counter_1 (
    .count(1'b1), .Q(counter_1_q), .clk(clock_1_out));  // open: load, D, carry, clr
  Clock clock_1 (.out(clock_1_out));
  ROM #(.addrWidth(7), .dataWidth(16)) rom_1 (.addr(counter_1_q), .data(rom_1_data), .sel(1'b1));
  ROM #(.addrWidth(7), .dataWidth(16)) rom_2 (.addr(counter_1_q), .data(rom_2_data), .sel(1'b1));
  RAM #(.addrWidth(7), .dataWidth(16)) ram_1 (
    .addr(counter_1_q), .data(ram_1_data), .sel(1'b1), .clk(clock_1_out), .ld(1'b0));  // open: clr
  alu_arithmetic alu_arithmetic_1 (
    .Set(in_2), .SetUnsigned(in_3), .Sub(in_1), .Output(ram_1_data), .in_4(rom_2_data), .in_5(rom_1_data));  // open: Overflow, Zero

  // Notes on the sheet:
  //   contents of rom_2 (hex, n*v repeats v):
  //   5d9a 3f44 855e a3a1 d28 2223 18c6 9c82 59d0 73d3 b3f8 41a 84f7 46e8 10b 671e 99c8 480 a4a9 b10 7735
  //   6d1f ca4 c614 b382 f284 1581 4aed 4f1d b0d5 e7bc 66f3 cf8 4fb0 22e0 d406 e071 43d6 efdc 543f a7e5
  //   e362 8d4c 6141 b428 7804 657c 1b6a ec63 891f 396e 4593 8060 335b f47 96b0 7819 9a50 6841 8f5 b4b
  //   988d da3f 7d96 faef 88e7 b4f6 102d 984a 2f1e 1e1b 627b 5d52 4e5a 2e3d f995 915d cf47 d274 33d9 e07e
  //   87bb 3542 7371 abf9 fa0d cd13 2987 7c46 b9b1 2df4 6f53 bed2 557 1eab 71d7 cdf5 ad30 6c56 6b81
endmodule
